// Logisim project 2BitMaxSelect.circ as structural Verilog: 1 circuit, main circuit main
module main (
  input  [1:0] A,
  input  [1:0] B,
  output [1:0] C
);

  wire and_1_out, and_2_out, and_3_out, and_4_out, not_1_out, not_2_out;

  not not_1 (not_1_out, A[1]);
  not not_2 (not_2_out, B[1]);
  or or_1 (C[1], A[1], B[1]);
  and and_1 (and_1_out, A[0], A[1]);
  and and_2 (and_2_out, B[0], B[1]);
  and and_3 (and_3_out, not_1_out, B[0]);
  and and_4 (and_4_out, A[0], not_2_out);
  or or_2 (C[0], and_1_out, and_2_out, and_3_out, and_4_out);

  // Notes on the sheet:
  //   A0
  //   A1
  //   B0
  //   B1
  //   A1+B1
  //   A1'B0
  //   A1A0
  //   B1B0
  //   A0B1'
  //   A1A0+B1B0+A1'B0+A0B1'
  //   C0
  //   C1
endmodule
