// Logisim project 2BitMaxSelectMux.circ as structural Verilog: 1 circuit, main circuit main
module main (
  input  [1:0] A,
  input  [1:0] B,
  output [1:0] out_3
);

  Multiplexer #(.select(4), .width(2), .enable("false")) multiplexer_1 (
    .in0(2'b00), .in1(2'b01), .in2(2'b10), .in3(2'b11), .in4(2'b01), .in5(2'b01), .in6(2'b10), .in7(2'b11),
    .in8(2'b10), .in9(2'b10), .in10(2'b10), .in11(2'b11), .in12(2'b11), .in13(2'b11), .in14(2'b11),
    .in15(2'b11), .out(out_3), .sel({B, A}));
endmodule
