// Logisim project Lab04.circ as structural Verilog: 5 circuits, main circuit Design1
module Design1 (
  input  [1:0] A,
  input  [1:0] B,
  output [1:0] C
);

  Multiplexer #(.select(4), .enable("false")) multiplexer_1 (
    .in0(1'b0), .in1(1'b0), .in2(1'b1), .in3(1'b1), .in4(1'b0), .in5(1'b0), .in6(1'b1), .in7(1'b1),
    .in8(1'b1), .in9(1'b1), .in10(1'b1), .in11(1'b1), .in12(1'b1), .in13(1'b1), .in14(1'b1), .in15(1'b1),
    .out(C[1]), .sel({B, A}));
  Multiplexer #(.select(4), .enable("false")) multiplexer_2 (
    .in0(1'b0), .in1(1'b1), .in2(1'b0), .in3(1'b1), .in4(1'b1), .in5(1'b1), .in6(1'b0), .in7(1'b1),
    .in8(1'b0), .in9(1'b0), .in10(1'b0), .in11(1'b1), .in12(1'b1), .in13(1'b1), .in14(1'b1), .in15(1'b1),
    .out(C[0]), .sel({B, A}));

  // Notes on the sheet:
  //   C1
  //   C0
endmodule

module Design_2 (
  input  [1:0] A,
  input  [1:0] B,
  output [1:0] C
);

  wire multiplexer_2_out, multiplexer_3_out, multiplexer_4_out, multiplexer_5_out, multiplexer_6_out,
       multiplexer_7_out;

  Multiplexer #(.enable("false")) multiplexer_1 (.in0(A[1]), .in1(B[1]), .out(C[1]), .sel(B[1]));
  Multiplexer #(.enable("false")) multiplexer_2 (.in0(A[0]), .in1(1'b0), .out(multiplexer_2_out), .sel(B[1]));
  Multiplexer #(.enable("false")) multiplexer_3 (.in0(B[0]), .in1(1'b0), .out(multiplexer_3_out), .sel(A[1]));
  Multiplexer #(.enable("false")) multiplexer_4 (.in0(1'b0), .in1(A[0]), .out(multiplexer_4_out), .sel(A[1]));
  Multiplexer #(.enable("false")) multiplexer_5 (.in0(1'b0), .in1(B[0]), .out(multiplexer_5_out), .sel(B[1]));
  Multiplexer #(.enable("false")) multiplexer_6 (
    .in0(multiplexer_2_out), .in1(multiplexer_3_out), .out(multiplexer_6_out), .sel(multiplexer_3_out));
  Multiplexer #(.enable("false")) multiplexer_7 (
    .in0(multiplexer_4_out), .in1(multiplexer_5_out), .out(multiplexer_7_out), .sel(multiplexer_5_out));
  Multiplexer #(.enable("false")) multiplexer_8 (
    .in0(multiplexer_6_out), .in1(multiplexer_7_out), .out(C[0]), .sel(multiplexer_7_out));

  // Notes on the sheet:
  //   B1'A0
  //   A1'B0
  //   A1A0
  //   B1B0
  //   If (A1 || B1 is one) return 1; Else return 0;
  //   If (B1 is one) return 0; Else return A0
  //   If (A1 is one) return 0; Else return B0
  //   If (A1 is one) return A0; Else return 0
  //   If (B1 is one) return B0; Else return 0
  //   If (A1 && B1 is one) return 0;
  //   Else if (A1 || B1 is one) return other bit 0;
  //   Else {If (A0 || B0 is one) return 1}
  //   B1'A0+A1'B0
  //   If (A1 || B1 is one) return their bit 0; Else return 0
  //   A1A0+B1B0
  //   (A1'B0+B1'A0)+(A1A0+B1B0)
endmodule

module Design_3 (
  input  [1:0] A,
  input  [1:0] B,
  output [1:0] C
);

  wire and_1_out, and_2_out, and_3_out, and_4_out, nand_2_out, nand_3_out, nand_4_out, nand_5_out,
       nand_7_out, nand_8_out, nand_9_out, nand_10_out, nand_11_out, nand_12_out, nand_13_out, nand_14_out,
       not_1_out, not_2_out;
  wire [1:0] nand_16_out, or_2_out, undriven, undriven_2, undriven_3, undriven_4;

  not not_1 (not_1_out, undriven[1]);
  or or_1 (or_2_out[1], undriven[1], undriven_2[1]);
  not not_2 (not_2_out, undriven_2[1]);
  and and_1 (and_1_out, undriven[0], undriven[1]);
  and and_2 (and_2_out, undriven_2[0], undriven_2[1]);
  and and_3 (and_3_out, not_1_out, undriven_2[0]);
  and and_4 (and_4_out, undriven[0], not_2_out);
  nand nand_1 (nand_16_out[1], ~undriven_3[1], ~undriven_4[1]);  // NAND_Gate
  nand nand_2 (nand_2_out, undriven_3[0], undriven_3[1]);
  nand nand_3 (nand_3_out, undriven_4[0], undriven_4[1]);
  nand nand_4 (nand_4_out, ~undriven_3[1], undriven_4[0]);  // NAND_Gate
  nand nand_5 (nand_5_out, undriven_3[0], ~undriven_4[1]);  // NAND_Gate
  nand nand_6 (C[1], ~A[1], ~B[1]);  // NAND_Gate
  nand nand_7 (nand_7_out, A[0], A[1]);
  nand nand_8 (nand_8_out, B[0], B[1]);
  nand nand_9 (nand_9_out, ~A[1], B[0]);  // NAND_Gate
  nand nand_10 (nand_10_out, A[0], ~B[1]);  // NAND_Gate
  or or_2 (or_2_out[0], and_1_out, and_2_out, and_3_out, and_4_out);
  nand nand_11 (nand_11_out, nand_2_out, nand_2_out);
  nand nand_12 (nand_12_out, nand_3_out, nand_3_out);
  nand nand_13 (nand_13_out, nand_4_out, nand_4_out);
  nand nand_14 (nand_14_out, nand_5_out, nand_5_out);
  nand nand_15 (C[0], nand_7_out, nand_8_out, nand_9_out, nand_10_out);
  nand nand_16 (nand_16_out[0], ~nand_11_out, ~nand_12_out, ~nand_13_out, ~nand_14_out);  // NAND_Gate

  // Notes on the sheet:
  //   A0
  //   A1
  //   B0
  //   B1
  //   A0
  //   A1
  //   B0
  //   B1
  //   A0
  //   A1
  //   B0
  //   B1
  //   A1+B1
  //   A1A0
  //   B1B0
  //   A1'B0
  //   A0B1'
  //   C0
  //   C1
  //   A1A0+B1B0+A1'B0+A0B1'
  //   Exactly the same as above but with only nand
  //   C0
  //   C1
  //   Simplified with bubble to bubble design
  //   C0
  //   C1
endmodule

module Design_4 (
  input  A,
  input  B,
  input  [1:0] IS,
  output RB,
  output [1:0] OS
);

  wire or_1_out;

  or or_1 (or_1_out, A, B);
  Multiplexer #(.select(2)) multiplexer_1 (
    .in0(or_1_out), .in1(A), .in2(B), .in3(or_1_out), .out(RB), .sel(IS));  // open: en
  Multiplexer #(.select(2), .width(2)) multiplexer_2 (
    .in0({B, A}), .in1(IS), .in2(IS), .in3({B, A}), .out(OS), .sel(IS));  // open: en

  // Notes on the sheet:
  //   Components of Design 4
  //   A: Bit from A
  //   B: Bit from B
  //   IS: Input Switch
  //   OS: Output Switch
  //   RB: Returned Bit
  //   Similar solution for returning the 2-bit number
  //   A switch (and input) that changes from default path to something similar to Design 2's check bit 0
  //   Default path: When not disabled, checks both input bits and returns 1 if either is on (an or gate)
  //   Realized that I wasn't limited to 2 input mux like I was in Design 2, so I used 4 input mux
  //   Switch should have 2-bit input and output to encode check both, check only A, check only B (potentially only 1 bit input/output is possible)
endmodule

module Design_5 (
  input  [3:0] A,
  input  [3:0] B,
  output [3:0] C
);

  wire [1:0] design_4_1_os, design_4_2_os, design_4_4_os;

  Design_4 design_4_1 (.A(A[3]), .B(B[3]), .IS(2'b00), .RB(C[3]), .OS(design_4_1_os));
  Design_4 design_4_2 (.A(A[2]), .B(B[2]), .IS(design_4_1_os), .RB(C[2]), .OS(design_4_2_os));
  Design_4 design_4_3 (.A(A[0]), .B(B[0]), .IS(design_4_4_os), .RB(C[0]));  // open: OS
  Design_4 design_4_4 (.A(A[1]), .B(B[1]), .IS(design_4_2_os), .RB(C[1]), .OS(design_4_4_os));

  // Notes on the sheet:
  //   Just linking up multiple Design 4s
endmodule
