// Logisim project Lab05.circ as structural Verilog: 4 circuits, main circuit Circuit 1
module Circuit_1 (
  input  IN,
  output SHOT
);

  wire clock_1_out, d_ff_1_q;

  Clock clock_1 (.out(clock_1_out));
  or or_1 (SHOT, IN, d_ff_1_q);
  D_Flip_Flop d_ff_1 (.clk(clock_1_out), .D(SHOT), .Q(d_ff_1_q));  // open: Qn, preset, en, reset
endmodule

module Circuit_2 (
  input  E,
  output T
);

  wire and_1_out, and_2_out, clock_1_out, d_ff_1_qn, not_1_out, or_1_out;

  Clock clock_1 (.out(clock_1_out));
  D_Flip_Flop d_ff_1 (.clk(clock_1_out), .D(or_1_out), .Q(T), .Qn(d_ff_1_qn));  // open: preset, en, reset
  not not_1 (not_1_out, E);
  and and_1 (and_1_out, not_1_out, T);
  and and_2 (and_2_out, d_ff_1_qn, E);
  or or_1 (or_1_out, and_1_out, and_2_out);
endmodule

module Circuit_3 (
  input  X,
  output UNLOCK
);

  wire and_1_out, and_2_out, and_3_out, and_5_out, clock_1_out, not_1_out, or_1_out, or_2_out, Q0_q, Q0_qn,
       Q1_q, Q1_qn;

  Clock clock_1 (.out(clock_1_out));
  not not_1 (not_1_out, X);
  D_Flip_Flop Q0 (.clk(clock_1_out), .D(or_2_out), .Q(Q0_q), .Qn(Q0_qn));  // open: preset, en, reset
  D_Flip_Flop Q1 (.clk(clock_1_out), .D(or_1_out), .Q(Q1_q), .Qn(Q1_qn));  // open: preset, en, reset
  and and_1 (and_1_out, X, Q0_qn);
  and and_2 (and_2_out, X, Q1_q);
  and and_3 (and_3_out, Q0_qn, Q1_q);
  and and_4 (UNLOCK, Q0_q, Q1_qn);
  and and_5 (and_5_out, Q1_q, not_1_out);
  or or_1 (or_1_out, and_1_out, and_2_out, and_3_out);
  or or_2 (or_2_out, UNLOCK, and_5_out);
endmodule

module test (
  input  X,
  output UNLOCK
);

  wire and_2_out, and_3_out, and_4_out, clock_1_out, not_1_out, or_1_out, or_2_out, Q0_q, Q0_qn, Q1_q, Q1_qn;

  Clock clock_1 (.out(clock_1_out));
  not not_1 (not_1_out, X);
  D_Flip_Flop Q0 (.clk(clock_1_out), .D(or_1_out), .Q(Q0_q), .Qn(Q0_qn));  // open: preset, en, reset
  D_Flip_Flop Q1 (.clk(clock_1_out), .D(or_2_out), .Q(Q1_q), .Qn(Q1_qn));  // open: preset, en, reset
  and and_1 (UNLOCK, Q1_qn, Q0_q);
  and and_2 (and_2_out, not_1_out, Q1_q);
  and and_3 (and_3_out, Q1_q, Q0_q);
  and and_4 (and_4_out, X, Q0_qn);
  or or_1 (or_1_out, UNLOCK, and_2_out);
  or or_2 (or_2_out, and_3_out, and_4_out);
endmodule
