// Logisim project Lab06.circ as structural Verilog: 1 circuit, main circuit Lab 6
module Lab_6 (
  input  Enable,
  input  A,
  input  B,
  output Valid,
  output Direction
);

  wire and_1_out, and_2_out, and_3_out, and_4_out, and_5_out, and_6_out, clock_1_out, D0_q, D0_qn, D1_qn,
       or_1_out, or_2_out;

  Clock clock_1 (.out(clock_1_out));
  and and_1 (and_1_out, Enable, Valid);
  and and_2 (and_2_out, Enable, D0_q, ~A, B);  // AND_Gate
  and and_3 (and_3_out, Enable, D0_q, A, ~B);  // AND_Gate
  and and_4 (and_4_out, Enable, D0_q, Valid);
  and and_5 (and_5_out, Enable, D0_q, ~A);  // AND_Gate
  and and_6 (and_6_out, Enable, D1_qn, ~A, ~B);  // AND_Gate
  or or_1 (or_1_out, and_1_out, and_2_out, and_3_out);
  or or_2 (or_2_out, and_4_out, and_5_out, and_6_out);
  D_Flip_Flop D1 (.clk(clock_1_out), .D(or_1_out), .Q(Valid), .Qn(D1_qn));  // open: preset, en, reset
  D_Flip_Flop D0 (.clk(clock_1_out), .D(or_2_out), .Q(D0_q), .Qn(D0_qn));  // open: preset, en, reset
  and and_7 (Direction, Valid, ~D0_q);  // AND_Gate

  // Notes on the sheet:
  //   Enable
  //   B
  //   Q1'
  //   A
  //   Q1
  //   Q0'
  //   Q0
endmodule
