// Logisim project Lab07.circ as structural Verilog: 3 circuits, main circuit Moore
module Figure_1 (
  input  in_1,
  input  in_2,
  input  in_3,
  input  in_4,
  output Q2_XOR_Q0__Q1,
  output out_6,
  output out_7
);

  wire and_1_out, and_2_out, and_4_out, and_5_out, and_6_out, and_7_out, clock_1_out, not_1_out, or_1_out,
       or_2_out, Q0_q, Q0_qn, Q1_q, Q1_qn, Q2_q, xor_1_out, xor_3_out;

  Clock clock_1 (.out(clock_1_out));
  not not_1 (not_1_out, in_1);
  xor xor_1 (xor_1_out, in_2, in_4);
  and and_1 (and_1_out, in_2, in_3);
  and and_2 (and_2_out, in_3, in_4);
  D_Flip_Flop Q0 (.clk(clock_1_out), .D(in_1), .Q(Q0_q), .Qn(Q0_qn));  // open: preset, en, reset
  D_Flip_Flop Q1 (.clk(clock_1_out), .D(or_1_out), .Q(Q1_q), .Qn(Q1_qn));  // open: preset, en, reset
  D_Flip_Flop Q2 (.clk(clock_1_out), .D(or_2_out), .Q(Q2_q));  // open: Qn, preset, en, reset
  and and_3 (out_6, xor_1_out, in_3);
  xor xor_2 (out_7, and_1_out, and_2_out);
  xor xor_3 (xor_3_out, Q0_q, Q2_q);
  and and_4 (and_4_out, Q2_q, Q1_qn, Q0_qn, in_1);
  and and_5 (and_5_out, Q0_q, not_1_out);
  and and_6 (and_6_out, Q1_q, Q0_qn);
  or or_1 (or_1_out, and_4_out, and_5_out);
  and and_7 (and_7_out, and_5_out, Q2_q);
  and and_8 (Q2_XOR_Q0__Q1, xor_3_out, Q1_q);
  or or_2 (or_2_out, and_7_out, and_6_out);

  // Notes on the sheet:
  //   Q0*=IN
  //   Q1*=Q2Q1'Q0'IN+Q0IN'
  //   Q2*=Q2Q0IN'+Q1Q0'
  //   Moore device
  //   1
  //   2
  //   UNLOCK=(Q2 XOR Q0) Q1
  //   CODES 1010, 1001(check)
  //   0
  //   Q2Q1'Q0'IN
  //   Q0IN'
  //   Q1Q0'
  //   Q2 XOR Q0
  //   Q2Q0IN'
  //   Q2Q1 XOR Q1Q0
  //   Q2Q1'Q0'IN+Q0IN'
  //   Q1*
  //   Q2*
  //   Q2Q0IN'+Q1Q0'
endmodule

module Moore (
  input  IN,
  output Unlock
);

  wire and_1_out, and_2_out, and_3_out, and_4_out, and_5_out, and_6_out, and_7_out, and_8_out, and_9_out,
       clock_1_out, not_1_out, or_1_out, or_2_out, Q0_q, Q0_qn, Q1_q, Q1_qn, Q2_q, Q2_qn;

  Clock clock_1 (.out(clock_1_out));
  not not_1 (not_1_out, IN);
  and and_1 (and_1_out, Q2_qn, Q0_q);
  and and_2 (and_2_out, Q2_q, Q1_q, IN);
  and and_3 (and_3_out, Q2_q, Q0_q, IN);
  and and_4 (and_4_out, Q1_q, Q0_qn, IN);
  and and_5 (and_5_out, Q2_q, Q0_qn, IN);
  and and_6 (and_6_out, Q1_q, Q0_q, not_1_out);
  and and_7 (and_7_out, Q2_q, Q0_q, not_1_out);
  or or_1 (or_1_out, and_1_out, and_2_out, and_3_out);
  or or_2 (or_2_out, and_4_out, and_5_out, and_6_out, and_7_out);
  D_Flip_Flop Q0 (.clk(clock_1_out), .D(IN), .Q(Q0_q), .Qn(Q0_qn));  // open: preset, en, reset
  D_Flip_Flop Q1 (.clk(clock_1_out), .D(or_1_out), .Q(Q1_q), .Qn(Q1_qn));  // open: preset, en, reset
  D_Flip_Flop Q2 (.clk(clock_1_out), .D(or_2_out), .Q(Q2_q), .Qn(Q2_qn));  // open: preset, en, reset
  and and_8 (and_8_out, Q0_q, Q1_q, Q2_q);
  and and_9 (and_9_out, Q0_qn, Q1_qn, Q2_q);
  or or_3 (Unlock, and_8_out, and_9_out);

  // Notes on the sheet:
  //   IN
  //   IN'
  //   Q0
  //   Q0'
  //   Q1
  //   Q1'
  //   Q2'
  //   Q2
  //   Q2'Q0
  //   Q2Q1IN
  //   Q2Q0IN
  //   Q1Q0'IN
  //   Q2Q0'IN
  //   Q2Q0IN'
  //   Q2Q0IN'
  //   Q2'Q0+Q2Q1IN+Q2Q0IN
  //   Q1Q0'IN+Q2Q0'IN+Q2Q0IN'+Q2Q0IN'
  //   IN
  //   Q2Q1Q0
  //   Q2Q1'Q0'
  //   Q2Q1Q0+Q2Q1'Q0'
endmodule

module Mealy (
  input  IN,
  output Unlock
);

  wire and_1_out, and_2_out, and_3_out, and_4_out, clock_1_out, not_1_out, or_1_out, Q0_q, Q0_qn, Q1_q,
       Q1_qn, Q2_q;

  Clock clock_1 (.out(clock_1_out));
  not not_1 (not_1_out, IN);
  and and_1 (and_1_out, Q1_q, Q0_qn, IN);
  and and_2 (and_2_out, Q1_q, Q0_q, not_1_out);
  and and_3 (and_3_out, Q2_q, Q0_qn, IN);
  and and_4 (and_4_out, Q2_q, Q0_q, not_1_out);
  or or_1 (or_1_out, and_1_out, and_2_out);
  or or_2 (Unlock, and_3_out, and_4_out);
  D_Flip_Flop Q0 (.clk(clock_1_out), .D(IN), .Q(Q0_q), .Qn(Q0_qn));  // open: preset, en, reset
  D_Flip_Flop Q1 (.clk(clock_1_out), .D(Q0_q), .Q(Q1_q), .Qn(Q1_qn));  // open: preset, en, reset
  D_Flip_Flop Q2 (.clk(clock_1_out), .D(or_1_out), .Q(Q2_q));  // open: Qn, preset, en, reset

  // Notes on the sheet:
  //   IN
  //   IN'
  //   Q0
  //   Q0'
  //   Q1
  //   Q1'
  //   Q1Q0'IN
  //   Q1Q0IN'
  //   Q2Q0'IN
  //   Q2Q0IN'
  //   Q2
  //   IN
  //   Q0
  //   Q1Q0'IN+Q1Q0IN'
  //   Q2Q0'IN+Q2Q0IN'
endmodule
