// Logisim project Lab10.circ as structural Verilog: 9 circuits, main circuit datapath (update it)
module datapath__update_it (
  input  [2:0] IN,
  input  Clock
);

  wire and_3_out, and_6_out, comparator_1_gt, comparator_1_lt, nand_1_out;
  wire [2:0] and_1_out, and_4_out, bitadder_1_out, FR_q, HL_q;

  and and_1 (and_1_out[0], IN[2], ~IN[1], ~IN[0]);  // AND_Gate
  and and_2 (and_1_out[1], IN[2], ~IN[1], IN[0]);  // AND_Gate
  and and_3 (and_3_out, IN[2], IN[1]);
  and and_4 (and_4_out[0], IN[2], IN[1], ~IN[0]);  // AND_Gate
  and and_5 (and_4_out[1], IN[2], IN[1], IN[0]);
  and and_6 (and_6_out, IN[2], ~IN[1]);  // AND_Gate
  or or_1 (and_1_out[2], ~IN[2], and_3_out);  // OR_Gate
  or or_2 (and_4_out[2], ~IN[2], and_6_out);  // OR_Gate
  Register #(.width(3)) HL (.D(and_1_out), .Q(HL_q), .clk(Clock));  // open: en, clr
  Register #(.width(3)) FR (.D(and_4_out), .Q(FR_q), .clk(Clock));  // open: en, clr
  LED HLG (.in(HL_q[0]));
  LED HLY (.in(HL_q[1]));
  LED HLR (.in(HL_q[2]));
  BitAdder #(.width(6)) bitadder_1 (.in0({FR_q, HL_q}), .out(bitadder_1_out));
  LED FLG (.in(FR_q[0]));
  LED FLY (.in(FR_q[1]));
  LED FLR (.in(FR_q[2]));
  Comparator #(.width(3)) comparator_1 (
    .a(bitadder_1_out), .b(3'b010), .gt(comparator_1_gt), .lt(comparator_1_lt));  // open: eq
  nand nand_1 (nand_1_out, comparator_1_lt, ~HL_q[0], ~HL_q[1], ~HL_q[2], ~FR_q[0], ~FR_q[1], ~FR_q[2]);  // NAND_Gate

  // Notes on the sheet:
  //   HL
  //   GYR GYR
  //   FR
endmodule

module Control_unit__update_it (
  input  Reset,
  input  CarDetect,
  output [2:0] OUT
);

  wire clock_1_out, comparator_1_eq, not_1_out, or_1_out;
  wire [1:0] multiplexer_2_out, tyellow_q;
  wire [1:1] multiplexer_1_out;
  wire [2:0] multiplexer_4_out, multiplexer_5_out, multiplexer_6_out, multiplexer_7_out, multiplexer_8_out,
       multiplexer_9_out;
  wire [4:0] trightofway_q;

  Clock clock_1 (.out(clock_1_out));
  Multiplexer #(.enable("false")) multiplexer_1 (.in0(1'b1), .in1(1'b0), .out(multiplexer_1_out[1]), .sel(or_1_out));
  or or_1 (or_1_out, Reset, not_1_out);
  Counter #(.width(2), .max('h2), .ongoal("stay")) tyellow (
    .load(or_1_out), .D({2{multiplexer_1_out[1]}}), .count(multiplexer_1_out[1]), .Q(tyellow_q),
    .clk(clock_1_out));  // open: carry, clr
  Counter #(.width(5), .max('h10), .ongoal("stay")) trightofway (
    .load(or_1_out), .D({5{multiplexer_1_out[1]}}), .count(multiplexer_1_out[1]), .Q(trightofway_q),
    .clk(clock_1_out));  // open: carry, clr
  Multiplexer #(.select(2), .enable("false")) multiplexer_2 (
    .in0(1'b0), .in1(1'b0), .in2(1'b1), .in3(1'b1), .out(multiplexer_2_out[0]), .sel(tyellow_q));
  Multiplexer #(.select(5), .enable("false")) multiplexer_3 (
    .in0(1'b0), .in1(1'b0), .in2(1'b0), .in3(1'b0), .in4(1'b0), .in5(1'b0), .in6(1'b0), .in7(1'b0),
    .in8(1'b0), .in9(1'b0), .in10(1'b0), .in11(1'b0), .in12(1'b0), .in13(1'b0), .in14(1'b0), .in15(1'b1),
    .in16(1'b1), .in17(1'b1), .in18(1'b1), .in19(1'b1), .in20(1'b1), .in21(1'b1), .in22(1'b1), .in23(1'b1),
    .in24(1'b1), .in25(1'b1), .in26(1'b1), .in27(1'b1), .in28(1'b1), .in29(1'b1), .in30(1'b1), .in31(1'b1),
    .out(multiplexer_2_out[1]), .sel(trightofway_q));
  Multiplexer #(.select(3), .width(3), .enable("false")) multiplexer_4 (
    .in0(3'b000), .in1(3'b000), .in2(3'b000), .in3(3'b000), .in4(3'b100), .in5(3'b110), .in6(3'b110),
    .in7(3'b100), .out(multiplexer_4_out), .sel(OUT));
  Multiplexer #(.select(3), .width(3), .enable("false")) multiplexer_5 (
    .in0(3'b100), .in1(3'b000), .in2(3'b000), .in3(3'b000), .in4(3'b100), .in5(3'b101), .in6(3'b111),
    .in7(3'b111), .out(multiplexer_5_out), .sel(OUT));
  Multiplexer #(.select(3), .width(3), .enable("false")) multiplexer_6 (
    .in0(3'b100), .in1(3'b000), .in2(3'b000), .in3(3'b000), .in4(3'b100), .in5(3'b110), .in6(3'b111),
    .in7(3'b100), .out(multiplexer_6_out), .sel(OUT));
  Multiplexer #(.select(3), .width(3), .enable("false")) multiplexer_7 (
    .in0(3'b100), .in1(3'b000), .in2(3'b000), .in3(3'b000), .in4(3'b101), .in5(3'b101), .in6(3'b111),
    .in7(3'b111), .out(multiplexer_7_out), .sel(OUT));
  Multiplexer #(.select(3), .width(3), .enable("false")) multiplexer_8 (
    .in0(3'b100), .in1(3'b000), .in2(3'b000), .in3(3'b000), .in4(3'b101), .in5(3'b110), .in6(3'b111),
    .in7(3'b100), .out(multiplexer_8_out), .sel(OUT));
  Multiplexer #(.select(4), .width(3), .enable("false")) multiplexer_9 (
    .in0(OUT), .in1(multiplexer_4_out), .in2(multiplexer_5_out), .in3(multiplexer_6_out), .in4(OUT),
    .in5(multiplexer_4_out), .in6(multiplexer_7_out), .in7(multiplexer_8_out), .in8(3'b000), .in9(3'b000),
    .in10(3'b000), .in11(3'b000), .in12(3'b000), .in13(3'b000), .in14(3'b000), .in15(3'b000),
    .out(multiplexer_9_out), .sel({Reset, CarDetect, multiplexer_2_out}));
  not not_1 (not_1_out, comparator_1_eq);
  Comparator #(.width(3)) comparator_1 (.a(OUT), .b(multiplexer_9_out), .eq(comparator_1_eq));  // open: gt, lt
  Register #(.width(3)) register_1 (.D(multiplexer_9_out), .Q(OUT), .clk(clock_1_out));  // open: en, clr
endmodule

module whole (
  input  Reset,
  input  CarDetect
);

  wire and_3_out, and_6_out, clock_1_out, comparator_1_eq, not_1_out, or_1_out;
  wire [1:0] multiplexer_2_out, tyellow_q;
  wire [1:1] multiplexer_1_out;
  wire [2:0] and_1_out, and_4_out, FR_q, HL_q, multiplexer_4_out, multiplexer_5_out, multiplexer_6_out,
       multiplexer_7_out, multiplexer_8_out, multiplexer_9_out, register_1_q;
  wire [4:0] trightofway_q;
  wire [5:0] PL_q;

  Clock clock_1 (.out(clock_1_out));
  Multiplexer #(.enable("false")) multiplexer_1 (.in0(1'b1), .in1(1'b0), .out(multiplexer_1_out[1]), .sel(or_1_out));
  or or_1 (or_1_out, Reset, not_1_out);
  Counter #(.width(2), .max('h2), .ongoal("stay")) tyellow (
    .load(or_1_out), .D({2{multiplexer_1_out[1]}}), .count(multiplexer_1_out[1]), .Q(tyellow_q),
    .clk(clock_1_out));  // open: carry, clr
  Counter #(.width(5), .max('h10), .ongoal("stay")) trightofway (
    .load(or_1_out), .D({5{multiplexer_1_out[1]}}), .count(multiplexer_1_out[1]), .Q(trightofway_q),
    .clk(clock_1_out));  // open: carry, clr
  Multiplexer #(.select(2), .enable("false")) multiplexer_2 (
    .in0(1'b0), .in1(1'b0), .in2(1'b1), .in3(1'b1), .out(multiplexer_2_out[0]), .sel(tyellow_q));
  Multiplexer #(.select(5), .enable("false")) multiplexer_3 (
    .in0(1'b0), .in1(1'b0), .in2(1'b0), .in3(1'b0), .in4(1'b0), .in5(1'b0), .in6(1'b0), .in7(1'b0),
    .in8(1'b0), .in9(1'b0), .in10(1'b0), .in11(1'b0), .in12(1'b0), .in13(1'b0), .in14(1'b0), .in15(1'b1),
    .in16(1'b1), .in17(1'b1), .in18(1'b1), .in19(1'b1), .in20(1'b1), .in21(1'b1), .in22(1'b1), .in23(1'b1),
    .in24(1'b1), .in25(1'b1), .in26(1'b1), .in27(1'b1), .in28(1'b1), .in29(1'b1), .in30(1'b1), .in31(1'b1),
    .out(multiplexer_2_out[1]), .sel(trightofway_q));
  Multiplexer #(.select(3), .width(3), .enable("false")) multiplexer_4 (
    .in0(3'b000), .in1(3'b000), .in2(3'b000), .in3(3'b000), .in4(3'b100), .in5(3'b110), .in6(3'b110),
    .in7(3'b100), .out(multiplexer_4_out), .sel(register_1_q));
  Multiplexer #(.select(3), .width(3), .enable("false")) multiplexer_5 (
    .in0(3'b100), .in1(3'b000), .in2(3'b000), .in3(3'b000), .in4(3'b100), .in5(3'b101), .in6(3'b111),
    .in7(3'b111), .out(multiplexer_5_out), .sel(register_1_q));
  Multiplexer #(.select(3), .width(3), .enable("false")) multiplexer_6 (
    .in0(3'b100), .in1(3'b000), .in2(3'b000), .in3(3'b000), .in4(3'b100), .in5(3'b110), .in6(3'b111),
    .in7(3'b100), .out(multiplexer_6_out), .sel(register_1_q));
  Multiplexer #(.select(3), .width(3), .enable("false")) multiplexer_7 (
    .in0(3'b100), .in1(3'b000), .in2(3'b000), .in3(3'b000), .in4(3'b101), .in5(3'b101), .in6(3'b111),
    .in7(3'b111), .out(multiplexer_7_out), .sel(register_1_q));
  Multiplexer #(.select(3), .width(3), .enable("false")) multiplexer_8 (
    .in0(3'b100), .in1(3'b000), .in2(3'b000), .in3(3'b000), .in4(3'b101), .in5(3'b110), .in6(3'b111),
    .in7(3'b100), .out(multiplexer_8_out), .sel(register_1_q));
  Multiplexer #(.select(4), .width(3), .enable("false")) multiplexer_9 (
    .in0(register_1_q), .in1(multiplexer_4_out), .in2(multiplexer_5_out), .in3(multiplexer_6_out),
    .in4(register_1_q), .in5(multiplexer_4_out), .in6(multiplexer_7_out), .in7(multiplexer_8_out),
    .in8(3'b000), .in9(3'b000), .in10(3'b000), .in11(3'b000), .in12(3'b000), .in13(3'b000), .in14(3'b000),
    .in15(3'b000), .out(multiplexer_9_out), .sel({Reset, CarDetect, multiplexer_2_out}));
  not not_1 (not_1_out, comparator_1_eq);
  Comparator #(.width(3)) comparator_1 (.a(register_1_q), .b(multiplexer_9_out), .eq(comparator_1_eq));  // open: gt, lt
  Register #(.width(3)) register_1 (.D(multiplexer_9_out), .Q(register_1_q), .clk(clock_1_out));  // open: en, clr
  and and_1 (and_1_out[0], register_1_q[2], ~register_1_q[1], ~register_1_q[0]);  // AND_Gate
  and and_2 (and_1_out[1], register_1_q[2], ~register_1_q[1], register_1_q[0]);  // AND_Gate
  or or_2 (and_1_out[2], ~register_1_q[2], and_3_out);  // OR_Gate
  and and_3 (and_3_out, register_1_q[2], register_1_q[1]);
  and and_4 (and_4_out[0], register_1_q[2], register_1_q[1], ~register_1_q[0]);  // AND_Gate
  and and_5 (and_4_out[1], register_1_q[2], register_1_q[1], register_1_q[0]);
  or or_3 (and_4_out[2], ~register_1_q[2], and_6_out);  // OR_Gate
  and and_6 (and_6_out, register_1_q[2], ~register_1_q[1]);  // AND_Gate
  LED HLG (.in(HL_q[0]));
  LED HLY (.in(HL_q[1]));
  Register #(.width(3)) HL (.D(and_1_out), .Q(HL_q), .clk(not_1_out));  // open: en, clr
  LED HLR (.in(HL_q[2]));
  LED FLG (.in(FR_q[0]));
  LED FLY (.in(FR_q[1]));
  Register #(.width(3)) FR (.D(and_4_out), .Q(FR_q), .clk(not_1_out));  // open: en, clr
  LED FLR (.in(FR_q[2]));
  Register #(.width(6)) PL (.D({FR_q, HL_q}), .Q(PL_q));  // open: en, clk, clr
endmodule

module datapath_2 (
  input  [2:0] IN,
  input  Clock,
  output HLG,
  output HLY,
  output HLR,
  output FLG,
  output FLY,
  output FLR,
  output Error_Check
);

  wire and_3_out, and_6_out, and_7_out, and_8_out, and_9_out, comparator_1_eq, nand_1_out, or_3_out, or_4_out;
  wire [2:0] and_1_out, and_4_out, bitadder_1_out;

  and and_1 (and_1_out[0], IN[2], ~IN[1], ~IN[0]);  // AND_Gate
  and and_2 (and_1_out[1], IN[2], ~IN[1], IN[0]);  // AND_Gate
  and and_3 (and_3_out, IN[2], IN[1]);
  and and_4 (and_4_out[0], IN[2], IN[1], ~IN[0]);  // AND_Gate
  and and_5 (and_4_out[1], IN[2], IN[1], IN[0]);
  and and_6 (and_6_out, IN[2], ~IN[1]);  // AND_Gate
  or or_1 (and_1_out[2], ~IN[2], and_3_out);  // OR_Gate
  or or_2 (and_4_out[2], ~IN[2], and_6_out);  // OR_Gate
  Register #(.width(3)) HL (.D(and_1_out), .Q({HLR, HLY, HLG}), .clk(Clock));  // open: en, clr
  Register #(.width(3)) FR (.D(and_4_out), .Q({FLR, FLY, FLG}), .clk(Clock));  // open: en, clr
  BitAdder #(.width(6)) bitadder_1 (.in0({FLR, FLY, FLG, HLR, HLY, HLG}), .out(bitadder_1_out));
  Comparator #(.width(3)) comparator_1 (.a(bitadder_1_out), .b(3'b010), .eq(comparator_1_eq));  // open: gt, lt
  or or_3 (or_3_out, HLG, HLY, HLR);
  or or_4 (or_4_out, FLY, FLG);
  and and_7 (and_7_out, or_3_out, ~FLG, ~FLY, FLR, comparator_1_eq);  // AND_Gate
  and and_8 (and_8_out, comparator_1_eq, ~HLG, ~HLY, HLR, or_4_out);  // AND_Gate
  and and_9 (and_9_out, ~and_7_out, ~and_8_out);  // AND_Gate
  nand nand_1 (nand_1_out, ~comparator_1_eq, ~HLG, ~HLY, ~HLR, ~FLG, ~FLY, ~FLR);  // NAND_Gate
  and and_10 (Error_Check, and_9_out, nand_1_out);

  // Notes on the sheet:
  //   HL
  //   GYR GYR
  //   FR
  //   For reset
endmodule

module proving_error_checking (
  input  HLG,
  input  HLY,
  input  HLR,
  input  FLG,
  input  FLY,
  input  FLR,
  output Error_Check
);

  wire and_1_out, and_2_out, and_3_out, comparator_1_eq, nand_1_out, or_1_out, or_2_out;
  wire [2:0] bitadder_1_out;

  BitAdder #(.width(6)) bitadder_1 (.in0({FLR, FLY, FLG, HLR, HLY, HLG}), .out(bitadder_1_out));
  Comparator #(.width(3)) comparator_1 (.a(bitadder_1_out), .b(3'b010), .eq(comparator_1_eq));  // open: gt, lt
  LED u_HLG (.in(HLG));
  LED u_HLY (.in(HLY));
  LED u_HLR (.in(HLR));
  LED u_FLG (.in(FLG));
  LED u_FLY (.in(FLY));
  LED u_FLR (.in(FLR));
  or or_1 (or_1_out, HLG, HLY, HLR);
  or or_2 (or_2_out, FLY, FLG);
  and and_1 (and_1_out, or_1_out, ~FLG, ~FLY, FLR, comparator_1_eq);  // AND_Gate
  and and_2 (and_2_out, comparator_1_eq, ~HLG, ~HLY, HLR, or_2_out);  // AND_Gate
  and and_3 (and_3_out, ~and_1_out, ~and_2_out);  // AND_Gate
  nand nand_1 (nand_1_out, ~comparator_1_eq, ~HLG, ~HLY, ~HLR, ~FLG, ~FLY, ~FLR);  // NAND_Gate
  and and_4 (Error_Check, and_3_out, nand_1_out);

  // Notes on the sheet:
  //   HL
  //   GYR GYR
  //   FR
  //   For reset
endmodule

module Control_unit_2 (
  input  Reset,
  input  CarDetect,
  input  Clock,
  input  Error_Check,
  output [2:0] Output
);

  wire comparator_1_eq, not_1_out, or_1_out;
  wire [1:0] tyellow_q;
  wire [1:1] multiplexer_1_out;
  wire [2:0] multiplexer_4_out, multiplexer_5_out, multiplexer_6_out, multiplexer_7_out, multiplexer_8_out,
       multiplexer_9_out, multiplexer_10_out, multiplexer_11_out, register_1_q;
  wire [3:0] multiplexer_2_out;
  wire [4:0] trightofway_q;

  Multiplexer #(.enable("false")) multiplexer_1 (.in0(1'b1), .in1(1'b0), .out(multiplexer_1_out[1]), .sel(or_1_out));
  or or_1 (or_1_out, Reset, not_1_out);
  or or_2 (multiplexer_2_out[3], Reset, Error_Check);
  Counter #(.width(2), .max('h2), .ongoal("stay")) tyellow (
    .load(or_1_out), .D({2{multiplexer_1_out[1]}}), .count(multiplexer_1_out[1]), .Q(tyellow_q), .clk(Clock));  // open: carry, clr
  Counter #(.width(5), .max('h10), .ongoal("stay")) trightofway (
    .load(or_1_out), .D({5{multiplexer_1_out[1]}}), .count(multiplexer_1_out[1]), .Q(trightofway_q),
    .clk(Clock));  // open: carry, clr
  Multiplexer #(.select(2), .enable("false")) multiplexer_2 (
    .in0(1'b0), .in1(1'b0), .in2(1'b1), .in3(1'b1), .out(multiplexer_2_out[0]), .sel(tyellow_q));
  Multiplexer #(.select(5), .enable("false")) multiplexer_3 (
    .in0(1'b0), .in1(1'b0), .in2(1'b0), .in3(1'b0), .in4(1'b0), .in5(1'b0), .in6(1'b0), .in7(1'b0),
    .in8(1'b0), .in9(1'b0), .in10(1'b0), .in11(1'b0), .in12(1'b0), .in13(1'b0), .in14(1'b0), .in15(1'b1),
    .in16(1'b1), .in17(1'b1), .in18(1'b1), .in19(1'b1), .in20(1'b1), .in21(1'b1), .in22(1'b1), .in23(1'b1),
    .in24(1'b1), .in25(1'b1), .in26(1'b1), .in27(1'b1), .in28(1'b1), .in29(1'b1), .in30(1'b1), .in31(1'b1),
    .out(multiplexer_2_out[1]), .sel(trightofway_q));
  Multiplexer #(.select(3), .width(3), .enable("false")) multiplexer_4 (
    .in0(3'b100), .in1(3'b000), .in2(3'b000), .in3(3'b000), .in4(3'b100), .in5(3'b000), .in6(3'b111),
    .in7(3'b111), .out(multiplexer_4_out), .sel(register_1_q));
  Multiplexer #(.select(3), .width(3), .enable("false")) multiplexer_5 (
    .in0(3'b100), .in1(3'b000), .in2(3'b000), .in3(3'b000), .in4(3'b100), .in5(3'b000), .in6(3'b111),
    .in7(3'b100), .out(multiplexer_5_out), .sel(register_1_q));
  Multiplexer #(.select(3), .width(3), .enable("false")) multiplexer_6 (
    .in0(3'b100), .in1(3'b000), .in2(3'b000), .in3(3'b000), .in4(3'b100), .in5(3'b000), .in6(3'b111),
    .in7(3'b111), .out(multiplexer_6_out), .sel(register_1_q));
  Multiplexer #(.select(3), .width(3), .enable("false")) multiplexer_7 (
    .in0(3'b100), .in1(3'b000), .in2(3'b000), .in3(3'b000), .in4(3'b100), .in5(3'b000), .in6(3'b111),
    .in7(3'b100), .out(multiplexer_7_out), .sel(register_1_q));
  Multiplexer #(.select(3), .width(3), .enable("false")) multiplexer_8 (
    .in0(3'b100), .in1(3'b000), .in2(3'b000), .in3(3'b000), .in4(3'b100), .in5(3'b101), .in6(3'b110),
    .in7(3'b111), .out(multiplexer_8_out), .sel(register_1_q));
  Multiplexer #(.select(3), .width(3), .enable("false")) multiplexer_9 (
    .in0(3'b100), .in1(3'b000), .in2(3'b000), .in3(3'b000), .in4(3'b100), .in5(3'b110), .in6(3'b110),
    .in7(3'b100), .out(multiplexer_9_out), .sel(register_1_q));
  Multiplexer #(.select(3), .width(3), .enable("false")) multiplexer_10 (
    .in0(3'b100), .in1(3'b000), .in2(3'b000), .in3(3'b000), .in4(3'b101), .in5(3'b101), .in6(3'b111),
    .in7(3'b111), .out(multiplexer_10_out), .sel(register_1_q));
  Multiplexer #(.select(3), .width(3), .enable("false")) multiplexer_11 (
    .in0(3'b100), .in1(3'b000), .in2(3'b000), .in3(3'b000), .in4(3'b101), .in5(3'b110), .in6(3'b111),
    .in7(3'b100), .out(multiplexer_11_out), .sel(register_1_q));
  Comparator #(.width(3)) comparator_1 (.a(register_1_q), .b(Output), .eq(comparator_1_eq));  // open: gt, lt
  Multiplexer #(.select(4), .width(3), .enable("false")) multiplexer_12 (
    .in0(multiplexer_4_out), .in1(multiplexer_5_out), .in2(multiplexer_6_out), .in3(multiplexer_7_out),
    .in4(multiplexer_8_out), .in5(multiplexer_9_out), .in6(multiplexer_10_out), .in7(multiplexer_11_out),
    .in8(3'b000), .in9(3'b000), .in10(3'b000), .in11(3'b000), .in12(3'b000), .in13(3'b000), .in14(3'b000),
    .in15(3'b000), .out(Output), .sel({multiplexer_2_out[3], CarDetect, multiplexer_2_out[1:0]}));
  Register #(.width(3)) register_1 (.D(Output), .Q(register_1_q), .clk(Clock));  // open: en, clr
  not not_1 (not_1_out, comparator_1_eq);

  // Notes on the sheet:
  //   Determine code based on previous state
  //   select
  //   code
  //   reset
  //   timer
endmodule

module whole_2 (
  input  Reset,
  input  CarDetect
);

  wire and_3_out, and_6_out, and_7_out, and_8_out, and_9_out, and_10_out, clock_1_out, comparator_1_eq,
       comparator_2_eq, nand_1_out, not_1_out, or_1_out, or_5_out, or_6_out;
  wire [1:0] tyellow_q;
  wire [1:1] multiplexer_1_out;
  wire [2:0] and_1_out, and_4_out, bitadder_1_out, FR_q, HL_q, multiplexer_4_out, multiplexer_5_out,
       multiplexer_6_out, multiplexer_7_out, multiplexer_8_out, multiplexer_9_out, multiplexer_10_out,
       multiplexer_11_out, multiplexer_12_out, register_1_q;
  wire [3:0] multiplexer_2_out;
  wire [4:0] trightofway_q;

  Multiplexer #(.enable("false")) multiplexer_1 (.in0(1'b1), .in1(1'b0), .out(multiplexer_1_out[1]), .sel(or_1_out));
  or or_1 (or_1_out, Reset, not_1_out);
  Clock clock_1 (.out(clock_1_out));
  or or_2 (multiplexer_2_out[3], Reset, and_10_out);
  Counter #(.width(2), .max('h2), .ongoal("stay")) tyellow (
    .load(or_1_out), .D({2{multiplexer_1_out[1]}}), .count(multiplexer_1_out[1]), .Q(tyellow_q),
    .clk(clock_1_out));  // open: carry, clr
  Counter #(.width(5), .max('h10), .ongoal("stay")) trightofway (
    .load(or_1_out), .D({5{multiplexer_1_out[1]}}), .count(multiplexer_1_out[1]), .Q(trightofway_q),
    .clk(clock_1_out));  // open: carry, clr
  Multiplexer #(.select(2), .enable("false")) multiplexer_2 (
    .in0(1'b0), .in1(1'b0), .in2(1'b1), .in3(1'b1), .out(multiplexer_2_out[0]), .sel(tyellow_q));
  Multiplexer #(.select(5), .enable("false")) multiplexer_3 (
    .in0(1'b0), .in1(1'b0), .in2(1'b0), .in3(1'b0), .in4(1'b0), .in5(1'b0), .in6(1'b0), .in7(1'b0),
    .in8(1'b0), .in9(1'b0), .in10(1'b0), .in11(1'b0), .in12(1'b0), .in13(1'b0), .in14(1'b0), .in15(1'b1),
    .in16(1'b1), .in17(1'b1), .in18(1'b1), .in19(1'b1), .in20(1'b1), .in21(1'b1), .in22(1'b1), .in23(1'b1),
    .in24(1'b1), .in25(1'b1), .in26(1'b1), .in27(1'b1), .in28(1'b1), .in29(1'b1), .in30(1'b1), .in31(1'b1),
    .out(multiplexer_2_out[1]), .sel(trightofway_q));
  Multiplexer #(.select(3), .width(3), .enable("false")) multiplexer_4 (
    .in0(3'b100), .in1(3'b000), .in2(3'b000), .in3(3'b000), .in4(3'b100), .in5(3'b000), .in6(3'b111),
    .in7(3'b111), .out(multiplexer_4_out), .sel(register_1_q));
  Multiplexer #(.select(3), .width(3), .enable("false")) multiplexer_5 (
    .in0(3'b100), .in1(3'b000), .in2(3'b000), .in3(3'b000), .in4(3'b100), .in5(3'b000), .in6(3'b111),
    .in7(3'b100), .out(multiplexer_5_out), .sel(register_1_q));
  Multiplexer #(.select(3), .width(3), .enable("false")) multiplexer_6 (
    .in0(3'b100), .in1(3'b000), .in2(3'b000), .in3(3'b000), .in4(3'b100), .in5(3'b000), .in6(3'b111),
    .in7(3'b111), .out(multiplexer_6_out), .sel(register_1_q));
  Multiplexer #(.select(3), .width(3), .enable("false")) multiplexer_7 (
    .in0(3'b100), .in1(3'b000), .in2(3'b000), .in3(3'b000), .in4(3'b100), .in5(3'b000), .in6(3'b111),
    .in7(3'b100), .out(multiplexer_7_out), .sel(register_1_q));
  Multiplexer #(.select(3), .width(3), .enable("false")) multiplexer_8 (
    .in0(3'b100), .in1(3'b000), .in2(3'b000), .in3(3'b000), .in4(3'b100), .in5(3'b101), .in6(3'b110),
    .in7(3'b111), .out(multiplexer_8_out), .sel(register_1_q));
  Multiplexer #(.select(3), .width(3), .enable("false")) multiplexer_9 (
    .in0(3'b100), .in1(3'b000), .in2(3'b000), .in3(3'b000), .in4(3'b100), .in5(3'b110), .in6(3'b110),
    .in7(3'b100), .out(multiplexer_9_out), .sel(register_1_q));
  Multiplexer #(.select(3), .width(3), .enable("false")) multiplexer_10 (
    .in0(3'b100), .in1(3'b000), .in2(3'b000), .in3(3'b000), .in4(3'b101), .in5(3'b101), .in6(3'b111),
    .in7(3'b111), .out(multiplexer_10_out), .sel(register_1_q));
  Multiplexer #(.select(3), .width(3), .enable("false")) multiplexer_11 (
    .in0(3'b100), .in1(3'b000), .in2(3'b000), .in3(3'b000), .in4(3'b101), .in5(3'b110), .in6(3'b111),
    .in7(3'b100), .out(multiplexer_11_out), .sel(register_1_q));
  Comparator #(.width(3)) comparator_1 (
    .a(register_1_q), .b(multiplexer_12_out), .eq(comparator_1_eq));  // open: gt, lt
  Multiplexer #(.select(4), .width(3), .enable("false")) multiplexer_12 (
    .in0(multiplexer_4_out), .in1(multiplexer_5_out), .in2(multiplexer_6_out), .in3(multiplexer_7_out),
    .in4(multiplexer_8_out), .in5(multiplexer_9_out), .in6(multiplexer_10_out), .in7(multiplexer_11_out),
    .in8(3'b000), .in9(3'b000), .in10(3'b000), .in11(3'b000), .in12(3'b000), .in13(3'b000), .in14(3'b000),
    .in15(3'b000), .out(multiplexer_12_out), .sel({multiplexer_2_out[3], CarDetect, multiplexer_2_out[1:0]}));
  Register #(.width(3)) register_1 (.D(multiplexer_12_out), .Q(register_1_q), .clk(clock_1_out));  // open: en, clr
  not not_1 (not_1_out, comparator_1_eq);
  and and_1 (and_1_out[0], multiplexer_12_out[2], ~multiplexer_12_out[1], ~multiplexer_12_out[0]);  // AND_Gate
  and and_2 (and_1_out[1], multiplexer_12_out[2], ~multiplexer_12_out[1], multiplexer_12_out[0]);  // AND_Gate
  and and_3 (and_3_out, multiplexer_12_out[2], multiplexer_12_out[1]);
  and and_4 (and_4_out[0], multiplexer_12_out[2], multiplexer_12_out[1], ~multiplexer_12_out[0]);  // AND_Gate
  and and_5 (and_4_out[1], multiplexer_12_out[2], multiplexer_12_out[1], multiplexer_12_out[0]);
  and and_6 (and_6_out, multiplexer_12_out[2], ~multiplexer_12_out[1]);  // AND_Gate
  or or_3 (and_1_out[2], ~multiplexer_12_out[2], and_3_out);  // OR_Gate
  or or_4 (and_4_out[2], ~multiplexer_12_out[2], and_6_out);  // OR_Gate
  Register #(.width(3)) HL (.D(and_1_out), .Q(HL_q), .clk(clock_1_out));  // open: en, clr
  Register #(.width(3)) FR (.D(and_4_out), .Q(FR_q), .clk(clock_1_out));  // open: en, clr
  BitAdder #(.width(6)) bitadder_1 (.in0({FR_q, HL_q}), .out(bitadder_1_out));
  Comparator #(.width(3)) comparator_2 (.a(bitadder_1_out), .b(3'b010), .eq(comparator_2_eq));  // open: gt, lt
  LED HLG (.in(HL_q[0]));
  LED HLY (.in(HL_q[1]));
  LED HLR (.in(HL_q[2]));
  LED FLG (.in(FR_q[0]));
  LED FLY (.in(FR_q[1]));
  LED FLR (.in(FR_q[2]));
  or or_5 (or_5_out, HL_q[0], HL_q[1], HL_q[2]);
  or or_6 (or_6_out, FR_q[1], FR_q[0]);
  and and_7 (and_7_out, or_5_out, ~FR_q[0], ~FR_q[1], FR_q[2], comparator_2_eq);  // AND_Gate
  and and_8 (and_8_out, ~and_7_out, ~and_9_out);  // AND_Gate
  and and_9 (and_9_out, comparator_2_eq, ~HL_q[0], ~HL_q[1], HL_q[2], or_6_out);  // AND_Gate
  nand nand_1 (nand_1_out, ~comparator_2_eq, ~HL_q[0], ~HL_q[1], ~HL_q[2], ~FR_q[0], ~FR_q[1], ~FR_q[2]);  // NAND_Gate
  and and_10 (and_10_out, and_8_out, nand_1_out);

  // Notes on the sheet:
  //   Determine code based on previous state
  //   select
  //   code
  //   reset
  //   timer
  //   HL
  //   FR
  //   GYR GYR
  //   Prevent Reset (default on for all unexpected states)
  //   Prevents valid farm road
  //   Prevents valid highway
  //   Prevents all off
endmodule

module Whole_2_boxes (
  input  Reset,
  input  Car_Detect
);

  wire clock_1_out, datapath_2_1_error_check, datapath_2_1_flg, datapath_2_1_flr, datapath_2_1_fly,
       datapath_2_1_hlg, datapath_2_1_hlr, datapath_2_1_hly;
  wire [2:0] control_unit_2_1_output;

  Clock clock_1 (.out(clock_1_out));
  Control_unit_2 control_unit_2_1 (
    .Reset(Reset), .CarDetect(Car_Detect), .Clock(clock_1_out), .Error_Check(datapath_2_1_error_check),
    .Output(control_unit_2_1_output));
  datapath_2 datapath_2_1 (
    .IN(control_unit_2_1_output), .Clock(clock_1_out), .Error_Check(datapath_2_1_error_check),
    .HLG(datapath_2_1_hlg), .HLY(datapath_2_1_hly), .HLR(datapath_2_1_hlr), .FLG(datapath_2_1_flg),
    .FLY(datapath_2_1_fly), .FLR(datapath_2_1_flr));
  LED HLG (.in(datapath_2_1_hlg));
  LED HLY (.in(datapath_2_1_hly));
  LED HLR (.in(datapath_2_1_hlr));
  LED FLG (.in(datapath_2_1_flg));
  LED FLY (.in(datapath_2_1_fly));
  LED FLR (.in(datapath_2_1_flr));
endmodule

module Whole_3__2_simplified (
  input  Reset,
  input  CarDetect
);

  wire and_3_out, and_6_out, and_7_out, and_8_out, and_9_out, clock_1_out, comparator_3_eq, comparator_4_eq,
       not_1_out, or_1_out, or_5_out, or_6_out;
  wire [1:0] tyellow_q;
  wire [1:1] multiplexer_1_out;
  wire [2:0] and_1_out, and_4_out, bitadder_1_out, FR_q, HL_q, multiplexer_2_out, multiplexer_3_out,
       multiplexer_4_out, multiplexer_5_out, multiplexer_6_out, multiplexer_7_out, multiplexer_8_out,
       multiplexer_9_out, multiplexer_10_out, register_1_q;
  wire [3:0] comparator_1_gt, trightofway_q;

  Multiplexer #(.enable("false")) multiplexer_1 (.in0(1'b1), .in1(1'b0), .out(multiplexer_1_out[1]), .sel(or_1_out));
  or or_1 (or_1_out, Reset, not_1_out);
  Clock clock_1 (.out(clock_1_out));
  or or_2 (comparator_1_gt[3], Reset, and_8_out);
  Counter #(.width(2), .max('h3), .ongoal("stay")) tyellow (
    .load(or_1_out), .D({2{multiplexer_1_out[1]}}), .count(multiplexer_1_out[1]), .Q(tyellow_q),
    .clk(clock_1_out));  // open: carry, clr
  Counter #(.width(4), .max('hf), .ongoal("stay")) trightofway (
    .load(or_1_out), .D({4{multiplexer_1_out[1]}}), .count(multiplexer_1_out[1]), .Q(trightofway_q),
    .clk(clock_1_out));  // open: carry, clr
  Comparator #(.width(2), .mode("unsigned")) comparator_1 (
    .a(tyellow_q), .b(2'b01), .gt(comparator_1_gt[0]));  // open: eq, lt
  Comparator #(.width(4), .mode("unsigned")) comparator_2 (
    .a(trightofway_q), .b(4'b1110), .gt(comparator_1_gt[1]));  // open: eq, lt
  Multiplexer #(.select(3), .width(3), .enable("false")) multiplexer_2 (
    .in0(3'b100), .in1(3'b000), .in2(3'b000), .in3(3'b000), .in4(3'b100), .in5(3'b000), .in6(3'b111),
    .in7(3'b111), .out(multiplexer_2_out), .sel(register_1_q));
  Multiplexer #(.select(3), .width(3), .enable("false")) multiplexer_3 (
    .in0(3'b100), .in1(3'b000), .in2(3'b000), .in3(3'b000), .in4(3'b100), .in5(3'b000), .in6(3'b111),
    .in7(3'b100), .out(multiplexer_3_out), .sel(register_1_q));
  Multiplexer #(.select(3), .width(3), .enable("false")) multiplexer_4 (
    .in0(3'b100), .in1(3'b000), .in2(3'b000), .in3(3'b000), .in4(3'b100), .in5(3'b000), .in6(3'b111),
    .in7(3'b111), .out(multiplexer_4_out), .sel(register_1_q));
  Multiplexer #(.select(3), .width(3), .enable("false")) multiplexer_5 (
    .in0(3'b100), .in1(3'b000), .in2(3'b000), .in3(3'b000), .in4(3'b100), .in5(3'b000), .in6(3'b111),
    .in7(3'b100), .out(multiplexer_5_out), .sel(register_1_q));
  Multiplexer #(.select(3), .width(3), .enable("false")) multiplexer_6 (
    .in0(3'b100), .in1(3'b000), .in2(3'b000), .in3(3'b000), .in4(3'b100), .in5(3'b101), .in6(3'b110),
    .in7(3'b111), .out(multiplexer_6_out), .sel(register_1_q));
  Multiplexer #(.select(3), .width(3), .enable("false")) multiplexer_7 (
    .in0(3'b100), .in1(3'b000), .in2(3'b000), .in3(3'b000), .in4(3'b100), .in5(3'b110), .in6(3'b110),
    .in7(3'b100), .out(multiplexer_7_out), .sel(register_1_q));
  Multiplexer #(.select(3), .width(3), .enable("false")) multiplexer_8 (
    .in0(3'b100), .in1(3'b000), .in2(3'b000), .in3(3'b000), .in4(3'b101), .in5(3'b101), .in6(3'b111),
    .in7(3'b111), .out(multiplexer_8_out), .sel(register_1_q));
  Multiplexer #(.select(3), .width(3), .enable("false")) multiplexer_9 (
    .in0(3'b100), .in1(3'b000), .in2(3'b000), .in3(3'b000), .in4(3'b101), .in5(3'b110), .in6(3'b111),
    .in7(3'b100), .out(multiplexer_9_out), .sel(register_1_q));
  Comparator #(.width(3)) comparator_3 (
    .a(register_1_q), .b(multiplexer_10_out), .eq(comparator_3_eq));  // open: gt, lt
  Multiplexer #(.select(4), .width(3), .enable("false")) multiplexer_10 (
    .in0(multiplexer_2_out), .in1(multiplexer_3_out), .in2(multiplexer_4_out), .in3(multiplexer_5_out),
    .in4(multiplexer_6_out), .in5(multiplexer_7_out), .in6(multiplexer_8_out), .in7(multiplexer_9_out),
    .in8(3'b000), .in9(3'b000), .in10(3'b000), .in11(3'b000), .in12(3'b000), .in13(3'b000), .in14(3'b000),
    .in15(3'b000), .out(multiplexer_10_out), .sel({comparator_1_gt[3], CarDetect, comparator_1_gt[1:0]}));
  Register #(.width(3)) register_1 (.D(multiplexer_10_out), .Q(register_1_q), .clk(clock_1_out));  // open: en, clr
  not not_1 (not_1_out, comparator_3_eq);
  and and_1 (and_1_out[0], multiplexer_10_out[2], ~multiplexer_10_out[1], ~multiplexer_10_out[0]);  // AND_Gate
  and and_2 (and_1_out[1], multiplexer_10_out[2], ~multiplexer_10_out[1], multiplexer_10_out[0]);  // AND_Gate
  and and_3 (and_3_out, multiplexer_10_out[2], multiplexer_10_out[1]);
  and and_4 (and_4_out[0], multiplexer_10_out[2], multiplexer_10_out[1], ~multiplexer_10_out[0]);  // AND_Gate
  and and_5 (and_4_out[1], multiplexer_10_out[2], multiplexer_10_out[1], multiplexer_10_out[0]);
  and and_6 (and_6_out, multiplexer_10_out[2], ~multiplexer_10_out[1]);  // AND_Gate
  or or_3 (and_1_out[2], ~multiplexer_10_out[2], and_3_out);  // OR_Gate
  or or_4 (and_4_out[2], ~multiplexer_10_out[2], and_6_out);  // OR_Gate
  Register #(.width(3)) HL (.D(and_1_out), .Q(HL_q), .clk(clock_1_out));  // open: en, clr
  Register #(.width(3)) FR (.D(and_4_out), .Q(FR_q), .clk(clock_1_out));  // open: en, clr
  BitAdder #(.width(6)) bitadder_1 (.in0({FR_q, HL_q}), .out(bitadder_1_out));
  Comparator #(.width(3)) comparator_4 (.a(bitadder_1_out), .b(3'b010), .eq(comparator_4_eq));  // open: gt, lt
  LED HLG (.in(HL_q[0]));
  LED HLY (.in(HL_q[1]));
  LED HLR (.in(HL_q[2]));
  LED FLG (.in(FR_q[0]));
  LED FLY (.in(FR_q[1]));
  LED FLR (.in(FR_q[2]));
  or or_5 (or_5_out, HL_q[0], HL_q[1], HL_q[2]);
  or or_6 (or_6_out, FR_q[1], FR_q[0]);
  and and_7 (and_7_out, or_5_out, ~FR_q[0], ~FR_q[1], FR_q[2], comparator_4_eq);  // AND_Gate
  and and_8 (and_8_out, ~and_7_out, ~and_9_out);  // AND_Gate
  and and_9 (and_9_out, comparator_4_eq, ~HL_q[0], ~HL_q[1], HL_q[2], or_6_out);  // AND_Gate

  // Notes on the sheet:
  //   Determine code based on previous state
  //   select
  //   code
  //   reset
  //   timer
  //   HL
  //   FR
  //   GYR GYR
  //   Prevent Reset (default on for all unexpected states)
  //   Prevents valid farm road
  //   Prevents valid highway
endmodule
