// Logisim project Lab11.circ as structural Verilog: 4 circuits, main circuit 8x4 RegFile
module _8x4_RegFile (
  input  [3:0] D_In,
  input  Write,
  input  [2:0] A_Addr,
  input  [2:0] D_Addr,
  input  [2:0] B_Addr,
  input  Clk,
  output [3:0] AOut,
  output [3:0] BOut
);

  wire and_1_out, and_2_out, and_3_out, and_4_out, and_5_out, and_6_out, and_7_out, and_8_out,
       decoder_1_out0, decoder_1_out1, decoder_1_out2, decoder_1_out3, decoder_1_out4, decoder_1_out5,
       decoder_1_out6, decoder_1_out7;
  wire [3:0] R0_q, R1_q, R2_q, R3_q, R4_q, R5_q, R6_q, R7_q;

  Decoder #(.select(3), .enable("false")) decoder_1 (
    .out0(decoder_1_out0), .out1(decoder_1_out1), .out2(decoder_1_out2), .out3(decoder_1_out3),
    .out4(decoder_1_out4), .out5(decoder_1_out5), .out6(decoder_1_out6), .out7(decoder_1_out7), .sel(D_Addr));
  and and_1 (and_1_out, Write, decoder_1_out0);
  and and_2 (and_2_out, Write, decoder_1_out1);
  and and_3 (and_3_out, Write, decoder_1_out2);
  and and_4 (and_4_out, Write, decoder_1_out3);
  and and_5 (and_5_out, Write, decoder_1_out4);
  and and_6 (and_6_out, Write, decoder_1_out5);
  and and_7 (and_7_out, Write, decoder_1_out6);
  and and_8 (and_8_out, Write, decoder_1_out7);
  Register #(.width(4)) R0 (.D(D_In), .en(and_1_out), .Q(R0_q), .clk(Clk), .clr(1'b0));
  Register #(.width(4)) R1 (.D(D_In), .en(and_2_out), .Q(R1_q), .clk(Clk), .clr(1'b0));
  Register #(.width(4)) R2 (.D(D_In), .en(and_3_out), .Q(R2_q), .clk(Clk), .clr(1'b0));
  Register #(.width(4)) R3 (.D(D_In), .en(and_4_out), .Q(R3_q), .clk(Clk), .clr(1'b0));
  Register #(.width(4)) R4 (.D(D_In), .en(and_5_out), .Q(R4_q), .clk(Clk), .clr(1'b0));
  Register #(.width(4)) R5 (.D(D_In), .en(and_6_out), .Q(R5_q), .clk(Clk), .clr(1'b0));
  Register #(.width(4)) R6 (.D(D_In), .en(and_7_out), .Q(R6_q), .clk(Clk), .clr(1'b0));
  Register #(.width(4)) R7 (.D(D_In), .en(and_8_out), .Q(R7_q), .clk(Clk), .clr(1'b0));
  Multiplexer #(.select(3), .width(4), .enable("false")) multiplexer_1 (
    .in0(R0_q), .in1(R1_q), .in2(R2_q), .in3(R3_q), .in4(R4_q), .in5(R5_q), .in6(R6_q), .in7(R7_q),
    .out(AOut), .sel(A_Addr));
  Multiplexer #(.select(3), .width(4), .enable("false")) multiplexer_2 (
    .in0(R0_q), .in1(R1_q), .in2(R2_q), .in3(R3_q), .in4(R4_q), .in5(R5_q), .in6(R6_q), .in7(R7_q),
    .out(BOut), .sel(B_Addr));
endmodule

module Function_Select (
  input  [3:0] A,
  input  [3:0] B,
  input  [3:0] Function_Select,
  output [3:0] F,
  output [2:0] PZN
);

  wire [3:0] adder_1_out, adder_2_out, and_1_out, divider_1_out, multiplier_1_out, not_1_out, or_1_out,
       shifter_1_out, shifter_2_out, shifter_3_out, subtractor_1_out;

  Adder #(.width(4)) adder_1 (.a(A), .b(B), .out(adder_1_out));  // open: cin, cout
  Multiplier #(.width(4)) multiplier_1 (.a(A), .b(B), .out(multiplier_1_out));  // open: cin, cout
  assign not_1_out = ~A;  // NOT_Gate not_1, 4 bits wide
  assign and_1_out = A & B;  // AND_Gate and_1, 4 bits wide
  assign or_1_out = A | B;  // OR_Gate or_1, 4 bits wide
  Shifter #(.width(4)) shifter_1 (.in(A), .\dist (2'b01), .out(shifter_1_out));
  Shifter #(.width(4), .shift("ar")) shifter_2 (.in(A), .\dist (2'b01), .out(shifter_2_out));
  Subtractor #(.width(4)) subtractor_1 (.a(A), .b(B), .out(subtractor_1_out));  // open: bin, bout
  Divider #(.width(4)) divider_1 (.a(A), .b(B), .out(divider_1_out));  // open: upper, rem
  Shifter #(.width(4)) shifter_3 (.in(A), .\dist (2'b01), .out(shifter_3_out));
  Adder #(.width(4)) adder_2 (.a(not_1_out), .b(4'b0001), .out(adder_2_out));  // open: cin, cout
  Multiplexer #(.select(4), .width(4), .enable("false")) multiplexer_1 (
    .in0(4'b0000), .in1(4'b0001), .in2(A), .in3(B), .in4(adder_1_out), .in5(subtractor_1_out),
    .in6(multiplier_1_out), .in7(divider_1_out), .in8(not_1_out), .in9(and_1_out), .in10(or_1_out),
    .in11(adder_2_out), .in12(shifter_1_out), .in13(shifter_3_out), .in14(shifter_2_out), .out(F),
    .sel(Function_Select));  // open: in15
  Comparator #(.width(4)) comparator_1 (.a(F), .b(4'b0000), .gt(PZN[2]), .eq(PZN[1]), .lt(PZN[0]));
endmodule

module Datapath (
  input  [2:0] D_Address,
  input  RegfileWrite,
  input  CLK,
  input  [2:0] A_Address,
  input  [2:0] B_Address,
  input  [3:0] constIn,
  input  MuxB,
  input  [3:0] Function_Select,
  input  [3:0] DataIn,
  input  MuxF,
  output [3:0] AddrOut,
  output [3:0] DataOut,
  output [2:0] PZN
);

  wire [3:0] function_select_1_f, multiplexer_2_out, n8x4_regfile_1_bout;

  _8x4_RegFile u_8x4_regfile_1 (
    .D_In(multiplexer_2_out), .D_Addr(D_Address), .Write(RegfileWrite), .Clk(CLK), .A_Addr(A_Address),
    .B_Addr(B_Address), .AOut(AddrOut), .BOut(n8x4_regfile_1_bout));
  Multiplexer #(.width(4), .enable("false")) multiplexer_1 (
    .in0(n8x4_regfile_1_bout), .in1(constIn), .out(DataOut), .sel(MuxB));
  Function_Select function_select_1 (
    .A(AddrOut), .B(DataOut), .Function_Select(Function_Select), .F(function_select_1_f), .PZN(PZN));
  Multiplexer #(.width(4), .enable("false")) multiplexer_2 (
    .in0(function_select_1_f), .in1(DataIn), .out(multiplexer_2_out), .sel(MuxF));
endmodule

module Final_Datapath (
  input  CLK,
  input  [15:0] Instruction,
  input  [3:0] constIn,
  input  [3:0] DataIn,
  output [3:0] AddrOut,
  output [3:0] DataOut,
  output [2:0] PZN
);

  wire [3:0] function_select_1_f, multiplexer_2_out, n8x4_regfile_1_bout;

  _8x4_RegFile u_8x4_regfile_1 (
    .D_In(multiplexer_2_out), .D_Addr(Instruction[3:1]), .Write(Instruction[0]), .Clk(CLK),
    .A_Addr(Instruction[15:13]), .B_Addr(Instruction[11:9]), .AOut(AddrOut), .BOut(n8x4_regfile_1_bout));
  Multiplexer #(.width(4), .enable("false")) multiplexer_1 (
    .in0(n8x4_regfile_1_bout), .in1(constIn), .out(DataOut), .sel(Instruction[12]));
  Function_Select function_select_1 (
    .A(AddrOut), .B(DataOut), .Function_Select(Instruction[7:4]), .F(function_select_1_f), .PZN(PZN));
  Multiplexer #(.width(4), .enable("false")) multiplexer_2 (
    .in0(function_select_1_f), .in1(DataIn), .out(multiplexer_2_out), .sel(Instruction[8]));
endmodule
