// Logisim project Lab8.circ as structural Verilog: 1 circuit, main circuit main
module main (
  input  Go,
  input  [3:0] In,
  input  [1:0] F,
  output [3:0] Out
);

  wire clock_1_out, multiplexer_1_out;
  wire [1:1] d_ff_1_q;
  wire [3:0] adder_1_out, multiplexer_2_out, multiplier_1_out, subtractor_1_out;

  Clock clock_1 (.out(clock_1_out));
  Multiplexer #(.select(2), .enable("false")) multiplexer_1 (
    .in0(1'b0), .in1(Go), .in2(1'b0), .in3(1'b0), .out(multiplexer_1_out), .sel({d_ff_1_q[1], Go}));
  D_Flip_Flop d_ff_1 (.clk(clock_1_out), .D(Go), .Q(d_ff_1_q[1]));  // open: Qn, preset, en, reset
  Adder #(.width(4)) adder_1 (.a(Out), .b(In), .out(adder_1_out));  // open: cin, cout
  Subtractor #(.width(4)) subtractor_1 (.a(Out), .b(In), .out(subtractor_1_out));  // open: bin, bout
  Multiplier #(.width(4)) multiplier_1 (.a(Out), .b(In), .out(multiplier_1_out));  // open: cin, cout
  Multiplexer #(.select(2), .width(4), .enable("false")) multiplexer_2 (
    .in0(In), .in1(adder_1_out), .in2(subtractor_1_out), .in3(multiplier_1_out), .out(multiplexer_2_out),
    .sel(F));
  Register #(.width(4)) register_1 (
    .D(multiplexer_2_out), .en(multiplexer_1_out), .Q(Out), .clk(clock_1_out));  // open: clr
endmodule
