// Logisim project Lab9.circ as structural Verilog: 9 circuits, main circuit Datapath
module Datapath (
  input  [2:0] IN,
  input  Clock
);

  wire and_3_out, and_6_out;
  wire [2:0] and_1_out, and_4_out, FR_q, HL_q;
  wire [5:0] PL_q;

  and and_1 (and_1_out[0], IN[2], ~IN[1], ~IN[0]);  // AND_Gate
  and and_2 (and_1_out[1], IN[2], ~IN[1], IN[0]);  // AND_Gate
  and and_3 (and_3_out, IN[2], IN[1]);
  and and_4 (and_4_out[0], IN[2], IN[1], ~IN[0]);  // AND_Gate
  and and_5 (and_4_out[1], IN[2], IN[1], IN[0]);
  and and_6 (and_6_out, IN[2], ~IN[1]);  // AND_Gate
  or or_1 (and_1_out[2], ~IN[2], and_3_out);  // OR_Gate
  or or_2 (and_4_out[2], ~IN[2], and_6_out);  // OR_Gate
  Register #(.width(3)) HL (.D(and_1_out), .Q(HL_q), .clk(Clock));  // open: en, clr
  Register #(.width(3)) FR (.D(and_4_out), .Q(FR_q), .clk(Clock));  // open: en, clr
  LED HLG (.in(HL_q[0]));
  LED HLY (.in(HL_q[1]));
  LED HLR (.in(HL_q[2]));
  LED FLG (.in(FR_q[0]));
  LED FLY (.in(FR_q[1]));
  LED FLR (.in(FR_q[2]));
  Register #(.width(6)) PL (.D({FR_q, HL_q}), .Q(PL_q));  // open: en, clk, clr
endmodule

module control_3 (
  input  Reset,
  input  CarDetect,
  output [2:0] OUT
);

  wire clock_1_out, comparator_1_eq, not_1_out, or_1_out;
  wire [1:0] multiplexer_2_out, tyellow_q;
  wire [1:1] multiplexer_1_out;
  wire [2:0] multiplexer_4_out, multiplexer_5_out, multiplexer_6_out, multiplexer_7_out, multiplexer_8_out,
       multiplexer_9_out;
  wire [4:0] trightofway_q;

  Clock clock_1 (.out(clock_1_out));
  Multiplexer #(.enable("false")) multiplexer_1 (.in0(1'b1), .in1(1'b0), .out(multiplexer_1_out[1]), .sel(or_1_out));
  or or_1 (or_1_out, Reset, not_1_out);
  Counter #(.width(2), .max('h2), .ongoal("stay")) tyellow (
    .load(or_1_out), .D({2{multiplexer_1_out[1]}}), .count(multiplexer_1_out[1]), .Q(tyellow_q),
    .clk(clock_1_out));  // open: carry, clr
  Counter #(.width(5), .max('h10), .ongoal("stay")) trightofway (
    .load(or_1_out), .D({5{multiplexer_1_out[1]}}), .count(multiplexer_1_out[1]), .Q(trightofway_q),
    .clk(clock_1_out));  // open: carry, clr
  Multiplexer #(.select(2), .enable("false")) multiplexer_2 (
    .in0(1'b0), .in1(1'b0), .in2(1'b1), .in3(1'b1), .out(multiplexer_2_out[0]), .sel(tyellow_q));
  Multiplexer #(.select(5), .enable("false")) multiplexer_3 (
    .in0(1'b0), .in1(1'b0), .in2(1'b0), .in3(1'b0), .in4(1'b0), .in5(1'b0), .in6(1'b0), .in7(1'b0),
    .in8(1'b0), .in9(1'b0), .in10(1'b0), .in11(1'b0), .in12(1'b0), .in13(1'b0), .in14(1'b0), .in15(1'b1),
    .in16(1'b1), .in17(1'b1), .in18(1'b1), .in19(1'b1), .in20(1'b1), .in21(1'b1), .in22(1'b1), .in23(1'b1),
    .in24(1'b1), .in25(1'b1), .in26(1'b1), .in27(1'b1), .in28(1'b1), .in29(1'b1), .in30(1'b1), .in31(1'b1),
    .out(multiplexer_2_out[1]), .sel(trightofway_q));
  Multiplexer #(.select(3), .width(3), .enable("false")) multiplexer_4 (
    .in0(3'b000), .in1(3'b000), .in2(3'b000), .in3(3'b000), .in4(3'b100), .in5(3'b110), .in6(3'b110),
    .in7(3'b100), .out(multiplexer_4_out), .sel(OUT));
  Multiplexer #(.select(3), .width(3), .enable("false")) multiplexer_5 (
    .in0(3'b100), .in1(3'b000), .in2(3'b000), .in3(3'b000), .in4(3'b100), .in5(3'b101), .in6(3'b111),
    .in7(3'b111), .out(multiplexer_5_out), .sel(OUT));
  Multiplexer #(.select(3), .width(3), .enable("false")) multiplexer_6 (
    .in0(3'b100), .in1(3'b000), .in2(3'b000), .in3(3'b000), .in4(3'b100), .in5(3'b110), .in6(3'b111),
    .in7(3'b100), .out(multiplexer_6_out), .sel(OUT));
  Multiplexer #(.select(3), .width(3), .enable("false")) multiplexer_7 (
    .in0(3'b100), .in1(3'b000), .in2(3'b000), .in3(3'b000), .in4(3'b101), .in5(3'b101), .in6(3'b111),
    .in7(3'b111), .out(multiplexer_7_out), .sel(OUT));
  Multiplexer #(.select(3), .width(3), .enable("false")) multiplexer_8 (
    .in0(3'b100), .in1(3'b000), .in2(3'b000), .in3(3'b000), .in4(3'b101), .in5(3'b110), .in6(3'b111),
    .in7(3'b100), .out(multiplexer_8_out), .sel(OUT));
  Multiplexer #(.select(4), .width(3), .enable("false")) multiplexer_9 (
    .in0(OUT), .in1(multiplexer_4_out), .in2(multiplexer_5_out), .in3(multiplexer_6_out), .in4(OUT),
    .in5(multiplexer_4_out), .in6(multiplexer_7_out), .in7(multiplexer_8_out), .in8(3'b000), .in9(3'b000),
    .in10(3'b000), .in11(3'b000), .in12(3'b000), .in13(3'b000), .in14(3'b000), .in15(3'b000),
    .out(multiplexer_9_out), .sel({Reset, CarDetect, multiplexer_2_out}));
  not not_1 (not_1_out, comparator_1_eq);
  Comparator #(.width(3)) comparator_1 (.a(OUT), .b(multiplexer_9_out), .eq(comparator_1_eq));  // open: gt, lt
  Register #(.width(3)) register_1 (.D(multiplexer_9_out), .Q(OUT), .clk(clock_1_out));  // open: en, clr
endmodule

module Control (
  input  Reset,
  input  CarDetect,
  input  ResetCounter,
  output [2:0] OUT
);

  wire clock_1_out;
  wire [1:0] multiplexer_2_out, tyellow_q;
  wire [1:1] multiplexer_1_out;
  wire [2:0] multiplexer_4_out, multiplexer_5_out, multiplexer_6_out, multiplexer_7_out, multiplexer_8_out,
       multiplexer_9_out, register_1_q, register_2_q;
  wire [4:0] trightofway_q;

  Multiplexer #(.enable("false")) multiplexer_1 (
    .in0(1'b1), .in1(1'b0), .out(multiplexer_1_out[1]), .sel(ResetCounter));
  Clock clock_1 (.out(clock_1_out));
  Counter #(.width(2), .max('h1), .ongoal("stay")) tyellow (
    .load(ResetCounter), .D({2{multiplexer_1_out[1]}}), .count(multiplexer_1_out[1]), .Q(tyellow_q),
    .clk(clock_1_out));  // open: carry, clr
  Counter #(.width(5), .max('hd), .ongoal("stay")) trightofway (
    .load(ResetCounter), .D({5{multiplexer_1_out[1]}}), .count(multiplexer_1_out[1]), .Q(trightofway_q),
    .clk(clock_1_out));  // open: carry, clr
  Multiplexer #(.select(2), .enable("false")) multiplexer_2 (
    .in0(1'b1), .in1(1'b1), .in2(1'b1), .in3(1'b1), .out(multiplexer_2_out[0]), .sel(tyellow_q));
  Multiplexer #(.select(5), .enable("false")) multiplexer_3 (
    .in0(1'b0), .in1(1'b0), .in2(1'b0), .in3(1'b0), .in4(1'b0), .in5(1'b0), .in6(1'b0), .in7(1'b0),
    .in8(1'b0), .in9(1'b0), .in10(1'b0), .in11(1'b0), .in12(1'b0), .in13(1'b1), .in14(1'b1), .in15(1'b1),
    .in16(1'b1), .in17(1'b1), .in18(1'b1), .in19(1'b1), .in20(1'b1), .in21(1'b1), .in22(1'b1), .in23(1'b1),
    .in24(1'b1), .in25(1'b1), .in26(1'b1), .in27(1'b1), .in28(1'b1), .in29(1'b1), .in30(1'b1), .in31(1'b1),
    .out(multiplexer_2_out[1]), .sel(trightofway_q));
  Multiplexer #(.select(3), .width(3), .enable("false")) multiplexer_4 (
    .in0(3'b000), .in1(3'b000), .in2(3'b000), .in3(3'b000), .in4(3'b100), .in5(3'b110), .in6(3'b110),
    .in7(3'b100), .out(multiplexer_4_out), .sel(register_2_q));
  Multiplexer #(.select(3), .width(3), .enable("false")) multiplexer_5 (
    .in0(3'b100), .in1(3'b000), .in2(3'b000), .in3(3'b000), .in4(3'b100), .in5(3'b101), .in6(3'b111),
    .in7(3'b111), .out(multiplexer_5_out), .sel(register_2_q));
  Multiplexer #(.select(3), .width(3), .enable("false")) multiplexer_6 (
    .in0(3'b100), .in1(3'b000), .in2(3'b000), .in3(3'b000), .in4(3'b100), .in5(3'b110), .in6(3'b111),
    .in7(3'b100), .out(multiplexer_6_out), .sel(register_2_q));
  Multiplexer #(.select(3), .width(3), .enable("false")) multiplexer_7 (
    .in0(3'b100), .in1(3'b000), .in2(3'b000), .in3(3'b000), .in4(3'b101), .in5(3'b101), .in6(3'b111),
    .in7(3'b111), .out(multiplexer_7_out), .sel(register_2_q));
  Multiplexer #(.select(3), .width(3), .enable("false")) multiplexer_8 (
    .in0(3'b100), .in1(3'b000), .in2(3'b000), .in3(3'b000), .in4(3'b101), .in5(3'b110), .in6(3'b111),
    .in7(3'b100), .out(multiplexer_8_out), .sel(register_2_q));
  Register #(.width(3)) register_1 (.D(OUT), .Q(register_1_q), .clk(clock_1_out));  // open: en, clr
  Register #(.width(3)) register_2 (.D(register_1_q), .Q(register_2_q), .clk(clock_1_out));  // open: en, clr
  Multiplexer #(.select(4), .width(3), .enable("false")) multiplexer_9 (
    .in0(register_2_q), .in1(multiplexer_4_out), .in2(multiplexer_5_out), .in3(multiplexer_6_out),
    .in4(register_2_q), .in5(multiplexer_4_out), .in6(multiplexer_7_out), .in7(multiplexer_8_out),
    .in8(3'b000), .in9(3'b000), .in10(3'b000), .in11(3'b000), .in12(3'b000), .in13(3'b000), .in14(3'b000),
    .in15(3'b000), .out(multiplexer_9_out), .sel({Reset, CarDetect, multiplexer_2_out}));
  Register #(.width(3)) register_3 (.D(multiplexer_9_out), .Q(OUT), .clk(clock_1_out));  // open: en, clr
endmodule

module Whole (
  input  Reset,
  input  CarDetect
);

  wire and_3_out, and_6_out, clock_1_out, comparator_1_eq, not_1_out;
  wire [1:0] multiplexer_2_out, tyellow_q;
  wire [1:1] multiplexer_1_out;
  wire [2:0] FR_q, HL_q, multiplexer_4_out, multiplexer_5_out, multiplexer_6_out, multiplexer_7_out,
       multiplexer_8_out, multiplexer_9_out, register_1_q, register_2_q, register_3_q;
  wire [4:0] trightofway_q;
  wire [5:0] or_1_out, PL_q;

  Multiplexer #(.enable("false")) multiplexer_1 (.in0(1'b1), .in1(1'b0), .out(multiplexer_1_out[1]), .sel(not_1_out));
  Clock clock_1 (.out(clock_1_out));
  Counter #(.width(2), .max('h1), .ongoal("stay")) tyellow (
    .load(not_1_out), .D({2{multiplexer_1_out[1]}}), .count(multiplexer_1_out[1]), .Q(tyellow_q),
    .clk(clock_1_out));  // open: carry, clr
  Counter #(.width(5), .max('hd), .ongoal("stay")) trightofway (
    .load(not_1_out), .D({5{multiplexer_1_out[1]}}), .count(multiplexer_1_out[1]), .Q(trightofway_q),
    .clk(clock_1_out));  // open: carry, clr
  Multiplexer #(.select(2), .enable("false")) multiplexer_2 (
    .in0(1'b1), .in1(1'b1), .in2(1'b1), .in3(1'b1), .out(multiplexer_2_out[0]), .sel(tyellow_q));
  Multiplexer #(.select(5), .enable("false")) multiplexer_3 (
    .in0(1'b0), .in1(1'b0), .in2(1'b0), .in3(1'b0), .in4(1'b0), .in5(1'b0), .in6(1'b0), .in7(1'b0),
    .in8(1'b0), .in9(1'b0), .in10(1'b0), .in11(1'b0), .in12(1'b0), .in13(1'b1), .in14(1'b1), .in15(1'b1),
    .in16(1'b1), .in17(1'b1), .in18(1'b1), .in19(1'b1), .in20(1'b1), .in21(1'b1), .in22(1'b1), .in23(1'b1),
    .in24(1'b1), .in25(1'b1), .in26(1'b1), .in27(1'b1), .in28(1'b1), .in29(1'b1), .in30(1'b1), .in31(1'b1),
    .out(multiplexer_2_out[1]), .sel(trightofway_q));
  Register #(.width(3)) register_1 (.D(register_3_q), .Q(register_1_q), .clk(clock_1_out));  // open: en, clr
  Multiplexer #(.select(3), .width(3), .enable("false")) multiplexer_4 (
    .in0(3'b000), .in1(3'b000), .in2(3'b000), .in3(3'b000), .in4(3'b100), .in5(3'b110), .in6(3'b110),
    .in7(3'b100), .out(multiplexer_4_out), .sel(register_2_q));
  Multiplexer #(.select(3), .width(3), .enable("false")) multiplexer_5 (
    .in0(3'b100), .in1(3'b000), .in2(3'b000), .in3(3'b000), .in4(3'b100), .in5(3'b101), .in6(3'b111),
    .in7(3'b111), .out(multiplexer_5_out), .sel(register_2_q));
  Multiplexer #(.select(3), .width(3), .enable("false")) multiplexer_6 (
    .in0(3'b100), .in1(3'b000), .in2(3'b000), .in3(3'b000), .in4(3'b100), .in5(3'b110), .in6(3'b111),
    .in7(3'b100), .out(multiplexer_6_out), .sel(register_2_q));
  Multiplexer #(.select(3), .width(3), .enable("false")) multiplexer_7 (
    .in0(3'b100), .in1(3'b000), .in2(3'b000), .in3(3'b000), .in4(3'b101), .in5(3'b101), .in6(3'b111),
    .in7(3'b111), .out(multiplexer_7_out), .sel(register_2_q));
  Multiplexer #(.select(3), .width(3), .enable("false")) multiplexer_8 (
    .in0(3'b100), .in1(3'b000), .in2(3'b000), .in3(3'b000), .in4(3'b101), .in5(3'b110), .in6(3'b111),
    .in7(3'b100), .out(multiplexer_8_out), .sel(register_2_q));
  Register #(.width(3)) register_2 (.D(register_1_q), .Q(register_2_q), .clk(clock_1_out));  // open: en, clr
  Multiplexer #(.select(4), .width(3), .enable("false")) multiplexer_9 (
    .in0(register_2_q), .in1(multiplexer_4_out), .in2(multiplexer_5_out), .in3(multiplexer_6_out),
    .in4(register_2_q), .in5(multiplexer_4_out), .in6(multiplexer_7_out), .in7(multiplexer_8_out),
    .in8(3'b000), .in9(3'b000), .in10(3'b000), .in11(3'b000), .in12(3'b000), .in13(3'b000), .in14(3'b000),
    .in15(3'b000), .out(multiplexer_9_out), .sel({Reset, CarDetect, multiplexer_2_out}));
  Register #(.width(3)) register_3 (.D(multiplexer_9_out), .Q(register_3_q), .clk(clock_1_out));  // open: en, clr
  Register #(.width(3)) HL (.D(register_3_q), .Q(HL_q), .clk(clock_1_out));  // open: en, clr
  Register #(.width(3)) FR (.D(register_3_q), .Q(FR_q), .clk(clock_1_out));  // open: en, clr
  and and_1 (or_1_out[2], HL_q[2], ~HL_q[1], ~HL_q[0]);  // AND_Gate
  and and_2 (or_1_out[1], HL_q[2], ~HL_q[1], HL_q[0]);  // AND_Gate
  and and_3 (and_3_out, HL_q[2], HL_q[1]);
  and and_4 (or_1_out[5], FR_q[2], FR_q[1], ~FR_q[0]);  // AND_Gate
  and and_5 (or_1_out[4], FR_q[2], FR_q[1], FR_q[0]);
  and and_6 (and_6_out, FR_q[2], ~FR_q[1]);  // AND_Gate
  LED HLG (.in(or_1_out[2]));
  LED HLY (.in(or_1_out[1]));
  LED HLR (.in(or_1_out[0]));
  or or_1 (or_1_out[0], ~HL_q[2], and_3_out);  // OR_Gate
  LED FLG (.in(or_1_out[5]));
  LED FLY (.in(or_1_out[4]));
  or or_2 (or_1_out[3], ~FR_q[2], and_6_out);  // OR_Gate
  LED FLR (.in(or_1_out[3]));
  Register #(.width(6)) PL (.D(or_1_out), .Q(PL_q), .clk(clock_1_out));  // open: en, clr
  Comparator #(.width(6)) comparator_1 (.a(or_1_out), .b(PL_q), .eq(comparator_1_eq));  // open: gt, lt
  not not_1 (not_1_out, comparator_1_eq);
endmodule

module test (
  input  CarDetect,
  input  Reset
);

  wire and_3_out, and_6_out, clock_1_out, comparator_1_eq, d_ff_1_q, d_ff_2_q, not_1_out;
  wire [1:0] tyellow_q;
  wire [1:1] multiplexer_1_out;
  wire [2:0] FR_q, HL_q, multiplexer_4_out, multiplexer_5_out, multiplexer_6_out, multiplexer_7_out,
       multiplexer_8_out, multiplexer_9_out, or_2_out, or_3_out, register_1_q, register_2_q, register_3_q;
  wire [3:0] multiplexer_2_out;
  wire [4:0] trightofway_q;
  wire [5:0] PL_q;

  D_Flip_Flop d_ff_1 (.clk(clock_1_out), .D(Reset), .Q(d_ff_1_q));  // open: Qn, preset, en, reset
  or or_1 (multiplexer_2_out[3], Reset, d_ff_1_q, d_ff_2_q);
  D_Flip_Flop d_ff_2 (.clk(clock_1_out), .D(d_ff_1_q), .Q(d_ff_2_q));  // open: Qn, preset, en, reset
  Clock clock_1 (.out(clock_1_out));
  Multiplexer #(.enable("false")) multiplexer_1 (.in0(1'b1), .in1(1'b0), .out(multiplexer_1_out[1]), .sel(not_1_out));
  Counter #(.width(2), .max('h1), .ongoal("stay")) tyellow (
    .load(not_1_out), .D({2{multiplexer_1_out[1]}}), .count(multiplexer_1_out[1]), .Q(tyellow_q),
    .clk(clock_1_out));  // open: carry, clr
  Counter #(.width(5), .max('hd), .ongoal("stay")) trightofway (
    .load(not_1_out), .D({5{multiplexer_1_out[1]}}), .count(multiplexer_1_out[1]), .Q(trightofway_q),
    .clk(clock_1_out));  // open: carry, clr
  Multiplexer #(.select(2), .enable("false")) multiplexer_2 (
    .in0(1'b1), .in1(1'b1), .in2(1'b1), .in3(1'b1), .out(multiplexer_2_out[0]), .sel(tyellow_q));
  Multiplexer #(.select(5), .enable("false")) multiplexer_3 (
    .in0(1'b0), .in1(1'b0), .in2(1'b0), .in3(1'b0), .in4(1'b0), .in5(1'b0), .in6(1'b0), .in7(1'b0),
    .in8(1'b0), .in9(1'b0), .in10(1'b0), .in11(1'b0), .in12(1'b0), .in13(1'b1), .in14(1'b1), .in15(1'b1),
    .in16(1'b1), .in17(1'b1), .in18(1'b1), .in19(1'b1), .in20(1'b1), .in21(1'b1), .in22(1'b1), .in23(1'b1),
    .in24(1'b1), .in25(1'b1), .in26(1'b1), .in27(1'b1), .in28(1'b1), .in29(1'b1), .in30(1'b1), .in31(1'b1),
    .out(multiplexer_2_out[1]), .sel(trightofway_q));
  Multiplexer #(.select(3), .width(3), .enable("false")) multiplexer_4 (
    .in0(3'b000), .in1(3'b000), .in2(3'b000), .in3(3'b000), .in4(3'b100), .in5(3'b110), .in6(3'b110),
    .in7(3'b100), .out(multiplexer_4_out), .sel(register_2_q));
  Multiplexer #(.select(3), .width(3), .enable("false")) multiplexer_5 (
    .in0(3'b100), .in1(3'b000), .in2(3'b000), .in3(3'b000), .in4(3'b100), .in5(3'b101), .in6(3'b111),
    .in7(3'b111), .out(multiplexer_5_out), .sel(register_2_q));
  Multiplexer #(.select(3), .width(3), .enable("false")) multiplexer_6 (
    .in0(3'b100), .in1(3'b000), .in2(3'b000), .in3(3'b000), .in4(3'b100), .in5(3'b110), .in6(3'b111),
    .in7(3'b100), .out(multiplexer_6_out), .sel(register_2_q));
  Multiplexer #(.select(3), .width(3), .enable("false")) multiplexer_7 (
    .in0(3'b100), .in1(3'b000), .in2(3'b000), .in3(3'b000), .in4(3'b101), .in5(3'b101), .in6(3'b111),
    .in7(3'b111), .out(multiplexer_7_out), .sel(register_2_q));
  Multiplexer #(.select(3), .width(3), .enable("false")) multiplexer_8 (
    .in0(3'b100), .in1(3'b000), .in2(3'b000), .in3(3'b000), .in4(3'b101), .in5(3'b110), .in6(3'b111),
    .in7(3'b100), .out(multiplexer_8_out), .sel(register_2_q));
  Register #(.width(3)) register_1 (.D(register_3_q), .Q(register_1_q), .clk(clock_1_out));  // open: en, clr
  Register #(.width(3)) register_2 (.D(register_1_q), .Q(register_2_q), .clk(clock_1_out));  // open: en, clr
  Register #(.width(3)) register_3 (.D(multiplexer_9_out), .Q(register_3_q), .clk(clock_1_out));  // open: en, clr
  Multiplexer #(.select(4), .width(3), .enable("false")) multiplexer_9 (
    .in0(register_2_q), .in1(multiplexer_4_out), .in2(multiplexer_5_out), .in3(multiplexer_6_out),
    .in4(register_2_q), .in5(multiplexer_4_out), .in6(multiplexer_7_out), .in7(multiplexer_8_out),
    .in8(3'b000), .in9(3'b000), .in10(3'b000), .in11(3'b000), .in12(3'b000), .in13(3'b000), .in14(3'b000),
    .in15(3'b000), .out(multiplexer_9_out), .sel({multiplexer_2_out[3], CarDetect, multiplexer_2_out[1:0]}));
  Register #(.width(3)) HL (.D(register_3_q), .Q(HL_q), .clk(clock_1_out));  // open: en, clr
  Register #(.width(3)) FR (.D(register_3_q), .Q(FR_q), .clk(clock_1_out));  // open: en, clr
  and and_1 (or_2_out[2], HL_q[2], ~HL_q[1], ~HL_q[0]);  // AND_Gate
  and and_2 (or_2_out[1], HL_q[2], ~HL_q[1], HL_q[0]);  // AND_Gate
  and and_3 (and_3_out, HL_q[2], HL_q[1]);
  and and_4 (or_3_out[2], FR_q[2], FR_q[1], ~FR_q[0]);  // AND_Gate
  and and_5 (or_3_out[1], FR_q[2], FR_q[1], FR_q[0]);
  and and_6 (and_6_out, FR_q[2], ~FR_q[1]);  // AND_Gate
  or or_2 (or_2_out[0], ~HL_q[2], and_3_out);  // OR_Gate
  or or_3 (or_3_out[0], ~FR_q[2], and_6_out);  // OR_Gate
  LED HLG (.in(or_2_out[2]));
  LED HLY (.in(or_2_out[1]));
  LED HLR (.in(or_2_out[0]));
  LED FLG (.in(or_3_out[2]));
  LED FLY (.in(or_3_out[1]));
  LED FLR (.in(or_3_out[0]));
  Register #(.width(6)) PL (.D({or_3_out, or_2_out}), .Q(PL_q), .clk(clock_1_out));  // open: en, clr
  Comparator #(.width(6)) comparator_1 (.a({or_3_out, or_2_out}), .b(PL_q), .eq(comparator_1_eq));  // open: gt, lt
  not not_1 (not_1_out, comparator_1_eq);
endmodule

module control_2 (
  input  Reset,
  input  CarDetect,
  output [2:0] out_3
);

  wire clock_1_out, comparator_1_eq, d_ff_1_q, d_ff_2_q, not_1_out, or_1_out, undriven, undriven_2,
       undriven_4, undriven_5;
  wire [1:0] multiplexer_2_out, tyellow_q;
  wire [1:1] multiplexer_1_out;
  wire [2:0] multiplexer_4_out, multiplexer_5_out, multiplexer_6_out, multiplexer_7_out, multiplexer_8_out,
       multiplexer_9_out, register_1_q, register_2_q, undriven_3;
  wire [4:0] trightofway_q;

  D_Flip_Flop d_ff_1 (.clk(undriven_2), .D(undriven), .Q(d_ff_1_q));  // open: Qn, preset, en, reset
  Clock clock_1 (.out(clock_1_out));
  or or_1 (or_1_out, undriven, d_ff_1_q, d_ff_2_q);
  D_Flip_Flop d_ff_2 (.clk(undriven_2), .D(d_ff_1_q), .Q(d_ff_2_q));  // open: Qn, preset, en, reset
  Multiplexer #(.enable("false")) multiplexer_1 (.in0(1'b1), .in1(1'b0), .out(multiplexer_1_out[1]), .sel(not_1_out));
  Counter #(.width(2), .max('h2), .ongoal("stay")) tyellow (
    .load(not_1_out), .D({2{multiplexer_1_out[1]}}), .count(multiplexer_1_out[1]), .Q(tyellow_q),
    .clk(clock_1_out));  // open: carry, clr
  Counter #(.width(5), .max('h10), .ongoal("stay")) trightofway (
    .load(not_1_out), .D({5{multiplexer_1_out[1]}}), .count(multiplexer_1_out[1]), .Q(trightofway_q),
    .clk(clock_1_out));  // open: carry, clr
  Multiplexer #(.select(2), .enable("false")) multiplexer_2 (
    .in0(1'b0), .in1(1'b0), .in2(1'b0), .in3(1'b1), .out(multiplexer_2_out[0]), .sel(tyellow_q));
  Multiplexer #(.select(5), .enable("false")) multiplexer_3 (
    .in0(1'b0), .in1(1'b0), .in2(1'b0), .in3(1'b0), .in4(1'b0), .in5(1'b0), .in6(1'b0), .in7(1'b0),
    .in8(1'b0), .in9(1'b0), .in10(1'b0), .in11(1'b0), .in12(1'b0), .in13(1'b0), .in14(1'b0), .in15(1'b1),
    .in16(1'b1), .in17(1'b1), .in18(1'b1), .in19(1'b1), .in20(1'b1), .in21(1'b1), .in22(1'b1), .in23(1'b1),
    .in24(1'b1), .in25(1'b1), .in26(1'b1), .in27(1'b1), .in28(1'b1), .in29(1'b1), .in30(1'b1), .in31(1'b1),
    .out(multiplexer_2_out[1]), .sel(trightofway_q));
  Register #(.width(3)) register_1 (.D(register_2_q), .Q(register_1_q), .clk(undriven_5));  // open: en, clr
  Register #(.width(3)) register_2 (.D(undriven_3), .Q(register_2_q), .clk(undriven_4));  // open: en, clr
  Multiplexer #(.select(3), .width(3), .enable("false")) multiplexer_4 (
    .in0(3'b000), .in1(3'b000), .in2(3'b000), .in3(3'b000), .in4(3'b100), .in5(3'b110), .in6(3'b110),
    .in7(3'b100), .out(multiplexer_4_out), .sel(out_3));
  Multiplexer #(.select(3), .width(3), .enable("false")) multiplexer_5 (
    .in0(3'b100), .in1(3'b000), .in2(3'b000), .in3(3'b000), .in4(3'b100), .in5(3'b101), .in6(3'b111),
    .in7(3'b111), .out(multiplexer_5_out), .sel(out_3));
  Multiplexer #(.select(3), .width(3), .enable("false")) multiplexer_6 (
    .in0(3'b100), .in1(3'b000), .in2(3'b000), .in3(3'b000), .in4(3'b100), .in5(3'b110), .in6(3'b111),
    .in7(3'b100), .out(multiplexer_6_out), .sel(out_3));
  Multiplexer #(.select(3), .width(3), .enable("false")) multiplexer_7 (
    .in0(3'b100), .in1(3'b000), .in2(3'b000), .in3(3'b000), .in4(3'b101), .in5(3'b101), .in6(3'b111),
    .in7(3'b111), .out(multiplexer_7_out), .sel(out_3));
  Multiplexer #(.select(3), .width(3), .enable("false")) multiplexer_8 (
    .in0(3'b100), .in1(3'b000), .in2(3'b000), .in3(3'b000), .in4(3'b101), .in5(3'b110), .in6(3'b111),
    .in7(3'b100), .out(multiplexer_8_out), .sel(out_3));
  Multiplexer #(.select(4), .width(3), .enable("false")) multiplexer_9 (
    .in0(out_3), .in1(multiplexer_4_out), .in2(multiplexer_5_out), .in3(multiplexer_6_out), .in4(out_3),
    .in5(multiplexer_4_out), .in6(multiplexer_7_out), .in7(multiplexer_8_out), .in8(3'b000), .in9(3'b000),
    .in10(3'b000), .in11(3'b000), .in12(3'b000), .in13(3'b000), .in14(3'b000), .in15(3'b000),
    .out(multiplexer_9_out), .sel({Reset, CarDetect, multiplexer_2_out}));
  not not_1 (not_1_out, comparator_1_eq);
  Comparator #(.width(3)) comparator_1 (.a(out_3), .b(multiplexer_9_out), .eq(comparator_1_eq));  // open: gt, lt
  Register #(.width(3)) register_3 (.D(multiplexer_9_out), .Q(out_3), .clk(clock_1_out));  // open: en, clr
endmodule

module whole2 (
  input  Reset,
  input  CarDetect,
  output out_3
);

  wire and_1_out, and_2_out, and_3_out, and_4_out, and_5_out, and_6_out, comparator_1_eq, not_1_out,
       or_1_out, or_2_out;
  wire [1:0] multiplexer_2_out, tyellow_q;
  wire [1:1] multiplexer_1_out;
  wire [2:0] FR_q, HL_q, multiplexer_4_out, multiplexer_5_out, multiplexer_6_out, multiplexer_7_out,
       multiplexer_8_out, multiplexer_9_out, register_1_q;
  wire [4:0] trightofway_q;

  Clock clock_1 (.out(out_3));
  Multiplexer #(.enable("false")) multiplexer_1 (.in0(1'b1), .in1(1'b0), .out(multiplexer_1_out[1]), .sel(not_1_out));
  Counter #(.width(2), .max('h2), .ongoal("stay")) tyellow (
    .load(not_1_out), .D({2{multiplexer_1_out[1]}}), .count(multiplexer_1_out[1]), .Q(tyellow_q), .clk(out_3));  // open: carry, clr
  Counter #(.width(5), .max('h10), .ongoal("stay")) trightofway (
    .load(not_1_out), .D({5{multiplexer_1_out[1]}}), .count(multiplexer_1_out[1]), .Q(trightofway_q),
    .clk(out_3));  // open: carry, clr
  Multiplexer #(.select(2), .enable("false")) multiplexer_2 (
    .in0(1'b0), .in1(1'b0), .in2(1'b1), .in3(1'b1), .out(multiplexer_2_out[0]), .sel(tyellow_q));
  Multiplexer #(.select(5), .enable("false")) multiplexer_3 (
    .in0(1'b0), .in1(1'b0), .in2(1'b0), .in3(1'b0), .in4(1'b0), .in5(1'b0), .in6(1'b0), .in7(1'b0),
    .in8(1'b0), .in9(1'b0), .in10(1'b0), .in11(1'b0), .in12(1'b0), .in13(1'b0), .in14(1'b0), .in15(1'b1),
    .in16(1'b1), .in17(1'b1), .in18(1'b1), .in19(1'b1), .in20(1'b1), .in21(1'b1), .in22(1'b1), .in23(1'b1),
    .in24(1'b1), .in25(1'b1), .in26(1'b1), .in27(1'b1), .in28(1'b1), .in29(1'b1), .in30(1'b1), .in31(1'b1),
    .out(multiplexer_2_out[1]), .sel(trightofway_q));
  Multiplexer #(.select(3), .width(3), .enable("false")) multiplexer_4 (
    .in0(3'b000), .in1(3'b000), .in2(3'b000), .in3(3'b000), .in4(3'b100), .in5(3'b110), .in6(3'b110),
    .in7(3'b100), .out(multiplexer_4_out), .sel(register_1_q));
  Multiplexer #(.select(3), .width(3), .enable("false")) multiplexer_5 (
    .in0(3'b100), .in1(3'b000), .in2(3'b000), .in3(3'b000), .in4(3'b100), .in5(3'b101), .in6(3'b111),
    .in7(3'b111), .out(multiplexer_5_out), .sel(register_1_q));
  Multiplexer #(.select(3), .width(3), .enable("false")) multiplexer_6 (
    .in0(3'b100), .in1(3'b000), .in2(3'b000), .in3(3'b000), .in4(3'b100), .in5(3'b110), .in6(3'b111),
    .in7(3'b100), .out(multiplexer_6_out), .sel(register_1_q));
  Multiplexer #(.select(3), .width(3), .enable("false")) multiplexer_7 (
    .in0(3'b100), .in1(3'b000), .in2(3'b000), .in3(3'b000), .in4(3'b101), .in5(3'b101), .in6(3'b111),
    .in7(3'b111), .out(multiplexer_7_out), .sel(register_1_q));
  Multiplexer #(.select(3), .width(3), .enable("false")) multiplexer_8 (
    .in0(3'b100), .in1(3'b000), .in2(3'b000), .in3(3'b000), .in4(3'b101), .in5(3'b110), .in6(3'b111),
    .in7(3'b100), .out(multiplexer_8_out), .sel(register_1_q));
  Multiplexer #(.select(4), .width(3), .enable("false")) multiplexer_9 (
    .in0(register_1_q), .in1(multiplexer_4_out), .in2(multiplexer_5_out), .in3(multiplexer_6_out),
    .in4(register_1_q), .in5(multiplexer_4_out), .in6(multiplexer_7_out), .in7(multiplexer_8_out),
    .in8(3'b000), .in9(3'b000), .in10(3'b000), .in11(3'b000), .in12(3'b000), .in13(3'b000), .in14(3'b000),
    .in15(3'b000), .out(multiplexer_9_out), .sel({Reset, CarDetect, multiplexer_2_out}));
  Comparator #(.width(3)) comparator_1 (.a(register_1_q), .b(multiplexer_9_out), .eq(comparator_1_eq));  // open: gt, lt
  not not_1 (not_1_out, comparator_1_eq);
  Register #(.width(3)) register_1 (.D(multiplexer_9_out), .Q(register_1_q), .clk(out_3));  // open: en, clr
  Register #(.width(3)) HL (.D(register_1_q), .Q(HL_q), .clk(out_3));  // open: en, clr
  Register #(.width(3)) FR (.D(register_1_q), .Q(FR_q), .clk(out_3));  // open: en, clr
  and and_1 (and_1_out, HL_q[2], ~HL_q[1], ~HL_q[0]);  // AND_Gate
  and and_2 (and_2_out, HL_q[2], ~HL_q[1], HL_q[0]);  // AND_Gate
  and and_3 (and_3_out, HL_q[2], HL_q[1]);
  and and_4 (and_4_out, FR_q[2], FR_q[1], ~FR_q[0]);  // AND_Gate
  and and_5 (and_5_out, FR_q[2], FR_q[1], FR_q[0]);
  and and_6 (and_6_out, FR_q[2], ~FR_q[1]);  // AND_Gate
  LED HLG (.in(and_1_out));
  LED HLY (.in(and_2_out));
  LED HLR (.in(or_1_out));
  or or_1 (or_1_out, ~HL_q[2], and_3_out);  // OR_Gate
  LED FLG (.in(and_4_out));
  LED FLY (.in(and_5_out));
  LED FLR (.in(or_2_out));
  or or_2 (or_2_out, ~FR_q[2], and_6_out);  // OR_Gate
endmodule

module data_3 (
  input  [2:0] IN,
  input  Clock
);

  wire and_3_out, and_6_out;
  wire [2:0] and_1_out, and_4_out, FR_q, HL_q;

  and and_1 (and_1_out[0], IN[2], ~IN[1], ~IN[0]);  // AND_Gate
  and and_2 (and_1_out[1], IN[2], ~IN[1], IN[0]);  // AND_Gate
  and and_3 (and_3_out, IN[2], IN[1]);
  and and_4 (and_4_out[0], IN[2], IN[1], ~IN[0]);  // AND_Gate
  and and_5 (and_4_out[1], IN[2], IN[1], IN[0]);
  and and_6 (and_6_out, IN[2], ~IN[1]);  // AND_Gate
  or or_1 (and_1_out[2], ~IN[2], and_3_out);  // OR_Gate
  or or_2 (and_4_out[2], ~IN[2], and_6_out);  // OR_Gate
  LED HLG (.in(HL_q[0]));
  LED HLY (.in(HL_q[1]));
  Register #(.width(3)) HL (.D(and_1_out), .Q(HL_q), .clk(Clock));  // open: en, clr
  LED HLR (.in(HL_q[2]));
  LED FLG (.in(FR_q[0]));
  LED FLY (.in(FR_q[1]));
  Register #(.width(3)) FR (.D(and_4_out), .Q(FR_q), .clk(Clock));  // open: en, clr
  LED FLR (.in(FR_q[2]));
endmodule

module whole3 (
  input  Reset,
  input  CarDetect
);

  wire and_3_out, and_6_out, clock_1_out, comparator_1_eq, not_1_out, or_1_out;
  wire [1:0] multiplexer_2_out, tyellow_q;
  wire [1:1] multiplexer_1_out;
  wire [2:0] and_1_out, and_4_out, FR_q, HL_q, multiplexer_4_out, multiplexer_5_out, multiplexer_6_out,
       multiplexer_7_out, multiplexer_8_out, multiplexer_9_out, register_1_q;
  wire [4:0] trightofway_q;

  Clock clock_1 (.out(clock_1_out));
  Multiplexer #(.enable("false")) multiplexer_1 (.in0(1'b1), .in1(1'b0), .out(multiplexer_1_out[1]), .sel(or_1_out));
  or or_1 (or_1_out, Reset, not_1_out);
  Counter #(.width(2), .max('h2), .ongoal("stay")) tyellow (
    .load(or_1_out), .D({2{multiplexer_1_out[1]}}), .count(multiplexer_1_out[1]), .Q(tyellow_q),
    .clk(clock_1_out));  // open: carry, clr
  Counter #(.width(5), .max('h10), .ongoal("stay")) trightofway (
    .load(or_1_out), .D({5{multiplexer_1_out[1]}}), .count(multiplexer_1_out[1]), .Q(trightofway_q),
    .clk(clock_1_out));  // open: carry, clr
  Multiplexer #(.select(2), .enable("false")) multiplexer_2 (
    .in0(1'b0), .in1(1'b0), .in2(1'b1), .in3(1'b1), .out(multiplexer_2_out[0]), .sel(tyellow_q));
  Multiplexer #(.select(5), .enable("false")) multiplexer_3 (
    .in0(1'b0), .in1(1'b0), .in2(1'b0), .in3(1'b0), .in4(1'b0), .in5(1'b0), .in6(1'b0), .in7(1'b0),
    .in8(1'b0), .in9(1'b0), .in10(1'b0), .in11(1'b0), .in12(1'b0), .in13(1'b0), .in14(1'b0), .in15(1'b1),
    .in16(1'b1), .in17(1'b1), .in18(1'b1), .in19(1'b1), .in20(1'b1), .in21(1'b1), .in22(1'b1), .in23(1'b1),
    .in24(1'b1), .in25(1'b1), .in26(1'b1), .in27(1'b1), .in28(1'b1), .in29(1'b1), .in30(1'b1), .in31(1'b1),
    .out(multiplexer_2_out[1]), .sel(trightofway_q));
  Multiplexer #(.select(3), .width(3), .enable("false")) multiplexer_4 (
    .in0(3'b000), .in1(3'b000), .in2(3'b000), .in3(3'b000), .in4(3'b100), .in5(3'b110), .in6(3'b110),
    .in7(3'b100), .out(multiplexer_4_out), .sel(register_1_q));
  Multiplexer #(.select(3), .width(3), .enable("false")) multiplexer_5 (
    .in0(3'b100), .in1(3'b000), .in2(3'b000), .in3(3'b000), .in4(3'b100), .in5(3'b101), .in6(3'b111),
    .in7(3'b111), .out(multiplexer_5_out), .sel(register_1_q));
  Multiplexer #(.select(3), .width(3), .enable("false")) multiplexer_6 (
    .in0(3'b100), .in1(3'b000), .in2(3'b000), .in3(3'b000), .in4(3'b100), .in5(3'b110), .in6(3'b111),
    .in7(3'b100), .out(multiplexer_6_out), .sel(register_1_q));
  Multiplexer #(.select(3), .width(3), .enable("false")) multiplexer_7 (
    .in0(3'b100), .in1(3'b000), .in2(3'b000), .in3(3'b000), .in4(3'b101), .in5(3'b101), .in6(3'b111),
    .in7(3'b111), .out(multiplexer_7_out), .sel(register_1_q));
  Multiplexer #(.select(3), .width(3), .enable("false")) multiplexer_8 (
    .in0(3'b100), .in1(3'b000), .in2(3'b000), .in3(3'b000), .in4(3'b101), .in5(3'b110), .in6(3'b111),
    .in7(3'b100), .out(multiplexer_8_out), .sel(register_1_q));
  Multiplexer #(.select(4), .width(3), .enable("false")) multiplexer_9 (
    .in0(register_1_q), .in1(multiplexer_4_out), .in2(multiplexer_5_out), .in3(multiplexer_6_out),
    .in4(register_1_q), .in5(multiplexer_4_out), .in6(multiplexer_7_out), .in7(multiplexer_8_out),
    .in8(3'b000), .in9(3'b000), .in10(3'b000), .in11(3'b000), .in12(3'b000), .in13(3'b000), .in14(3'b000),
    .in15(3'b000), .out(multiplexer_9_out), .sel({Reset, CarDetect, multiplexer_2_out}));
  Comparator #(.width(3)) comparator_1 (.a(register_1_q), .b(multiplexer_9_out), .eq(comparator_1_eq));  // open: gt, lt
  not not_1 (not_1_out, comparator_1_eq);
  Register #(.width(3)) register_1 (.D(multiplexer_9_out), .Q(register_1_q), .clk(clock_1_out));  // open: en, clr
  and and_1 (and_1_out[0], register_1_q[2], ~register_1_q[1], ~register_1_q[0]);  // AND_Gate
  and and_2 (and_1_out[1], register_1_q[2], ~register_1_q[1], register_1_q[0]);  // AND_Gate
  and and_3 (and_3_out, register_1_q[2], register_1_q[1]);
  and and_4 (and_4_out[0], register_1_q[2], register_1_q[1], ~register_1_q[0]);  // AND_Gate
  and and_5 (and_4_out[1], register_1_q[2], register_1_q[1], register_1_q[0]);
  and and_6 (and_6_out, register_1_q[2], ~register_1_q[1]);  // AND_Gate
  or or_2 (and_1_out[2], ~register_1_q[2], and_3_out);  // OR_Gate
  or or_3 (and_4_out[2], ~register_1_q[2], and_6_out);  // OR_Gate
  Register #(.width(3)) HL (.D(and_1_out), .Q(HL_q), .clk(clock_1_out));  // open: en, clr
  Register #(.width(3)) FR (.D(and_4_out), .Q(FR_q), .clk(clock_1_out));  // open: en, clr
  LED HLG (.in(HL_q[0]));
  LED HLY (.in(HL_q[1]));
  LED HLR (.in(HL_q[2]));
  LED FLG (.in(FR_q[0]));
  LED FLY (.in(FR_q[1]));
  LED FLR (.in(FR_q[2]));
endmodule
